// Logisim project Piloufas.circ as structural Verilog: 14 circuits, main circuit main
module main (
);

  wire alarmer_1_sound, button_1_out, button_2_out, button_3_out, home, nxt, nxt_1, nxt_2, nxt_3, or_1_out,
       or_2_out, or_3_out, or_4_out, or_6_out, rst_sys, time_div_1_out_1;
  wire [3:0] output_display_1_o, output_display_1_o_2;
  wire [5:0] but_state, but_state_1, but_state_2, but_state_3, but_state_4;
  wire [23:0] D_alarm, D_chron, D_clock, D_timer;
  wire [23:8] output_display_1_o_3;

  Button button_1 (.out(button_1_out));
  Button button_2 (.out(button_2_out));
  Button button_3 (.out(button_3_out));
  Button button_4 (.out(rst_sys));
  buf or_1 (or_1_out, rst_sys);  // OR_Gate
  buf or_2 (or_2_out, rst_sys);  // OR_Gate
  // Probe on but_state
  button_input button_input_1 (.A(button_1_out), .B(button_2_out), .C(button_3_out), .but_o(but_state));  // open: R
  input_System input_system_1 (
    .b_i(but_state), .nxt(nxt), .R(or_1_out), .b_o_1(but_state_1), .b_o_2(but_state_2), .b_o_3(but_state_3),
    .b_o_4(but_state_4));
  // Probe on but_state_2
  alarmer alarmer_1 (
    .EN(1'b1), .R(or_2_out), .but_i(but_state_2), .t(D_clock), .o(D_alarm), .nxt(nxt_2), .rst(home),
    .sound(alarmer_1_sound));
  LED led_1 (.in(alarmer_1_sound));
  or or_3 (or_3_out, home, rst_sys);
  output_display output_display_1 (
    .i_1(D_clock), .i_2(D_alarm), .i_3(D_chron), .i_4(D_timer), .nxt(nxt), .R(or_3_out),
    .o({output_display_1_o_3, output_display_1_o_2, output_display_1_o}));
  time_div time_div_1 (.out_1(time_div_1_out_1));
  buf or_4 (or_4_out, rst_sys);  // OR_Gate
  Hex_Digit_Display hex_digit_display_1 (.value(output_display_1_o_3[23:20]));  // open: dp
  Hex_Digit_Display hex_digit_display_2 (.value(output_display_1_o_3[19:16]));  // open: dp
  or or_5 (nxt, nxt_1, nxt_2, nxt_3);
  buf or_6 (or_6_out, rst_sys);  // OR_Gate
  Hex_Digit_Display hex_digit_display_3 (.value(output_display_1_o_3[15:12]));  // open: dp
  // Probe on but_state_3
  Hex_Digit_Display hex_digit_display_4 (.value(output_display_1_o_3[11:8]));  // open: dp
  clocker2 clocker2_1 (.EN(time_div_1_out_1), .R(or_4_out), .but_i(but_state_1), .o(D_clock), .nxt(nxt_1), .rst(home));
  chronometer chronometer_1 (.R(or_6_out), .b_i(but_state_3), .o(D_chron), .nxt(nxt_3), .rst(home));
  Hex_Digit_Display hex_digit_display_5 (.value(output_display_1_o));  // open: dp
  Hex_Digit_Display hex_digit_display_6 (.value(output_display_1_o_2));  // open: dp
endmodule

module press (
  input  b_in,
  input  R,
  output st,
  output lg
);

  wire button_1_out, clock_1_out, counter_1_carry, counter_2_carry, counter_3_carry, d_ff_1_q, d_ff_2_q,
       not_1_out, not_2_out, not_3_out, or_1_out, or_2_out, or_3_out, or_4_out, or_5_out;

  Button button_1 (.out(button_1_out));
  or or_1 (or_1_out, b_in, button_1_out);
  D_Flip_Flop #(.trigger("falling")) d_ff_1 (
    .D(not_1_out), .clk(or_1_out), .Q(d_ff_1_q), .reset(or_4_out));  // open: Qn, preset
  not not_1 (not_1_out, counter_1_carry);
  D_Flip_Flop #(.trigger("falling")) d_ff_2 (
    .D(counter_1_carry), .clk(or_1_out), .Q(d_ff_2_q), .reset(or_4_out));  // open: Qn, preset
  or or_2 (or_2_out, counter_2_carry, R);
  or or_3 (or_3_out, or_1_out, R);
  or or_4 (or_4_out, R, counter_2_carry);
  Counter #(.width(6), .max('h10), .ongoal("stay")) counter_1 (
    .clr(or_2_out), .count(or_1_out), .clk(counter_3_carry), .carry(counter_1_carry));  // open: load, up, D, Q
  Counter #(.width(2), .max('h2), .ongoal("stay")) counter_2 (
    .clr(or_3_out), .count(or_5_out), .clk(counter_3_carry), .carry(counter_2_carry));  // open: load, up, D, Q
  Clock clock_1 (.out(clock_1_out));
  Counter #(.width(4), .max('h8)) counter_3 (
    .clk(clock_1_out), .carry(counter_3_carry));  // open: clr, load, up, count, D, Q
  or or_5 (or_5_out, d_ff_1_q, d_ff_2_q);
  not not_2 (not_2_out, counter_1_carry);
  not not_3 (not_3_out, d_ff_1_q);
  and and_1 (st, d_ff_1_q, not_2_out);
  and and_2 (lg, counter_1_carry, not_3_out);
endmodule

module button_input (
  input  A,
  input  B,
  input  C,
  input  R,
  output [5:0] but_o
);

  press press_1 (.b_in(A), .R(R), .st(but_o[0]), .lg(but_o[1]));
  press press_2 (.b_in(B), .R(R), .st(but_o[2]), .lg(but_o[3]));
  press press_3 (.b_in(C), .R(R), .st(but_o[4]), .lg(but_o[5]));

  // Notes on the sheet:
  //   Dans l'ordre de 0 à 5 : A_st | A_lg | B_st | B_lg | C_st | C_lg
endmodule

module output_display (
  input  [23:0] i_1,
  input  [23:0] i_2,
  input  [23:0] i_3,
  input  [23:0] i_4,
  input  nxt,
  input  R,
  output [23:0] o
);

  wire clock_1_out;
  wire [1:0] counter_1_q;

  Clock clock_1 (.out(clock_1_out));
  Counter #(.width(2), .max('h3)) counter_1 (
    .clr(R), .count(nxt), .clk(clock_1_out), .Q(counter_1_q));  // open: load, up, D, carry
  Multiplexer #(.select(2), .width(24), .enable("false")) multiplexer_1 (
    .in0(i_1), .in1(i_2), .in2(i_3), .in3(i_4), .out(o), .sel(counter_1_q));
endmodule

module count_to_sixty (
  input  EN,
  input  R,
  output [3:0] low,
  output [3:0] high,
  output c
);

  wire and_1_out, clock_1_out, counter_1_carry, counter_2_carry;

  Clock clock_1 (.out(clock_1_out));
  Counter #(.width(4), .max('h9)) counter_1 (
    .clr(R), .count(EN), .clk(clock_1_out), .carry(counter_1_carry), .Q(low));  // open: load, up, D
  Counter #(.width(4), .max('h5)) counter_2 (
    .clr(R), .count(and_1_out), .clk(clock_1_out), .carry(counter_2_carry), .Q(high));  // open: load, up, D
  and and_1 (and_1_out, counter_1_carry, EN);
  and and_2 (c, counter_2_carry, and_1_out);
endmodule

module count_to_twenty (
  input  EN,
  input  R,
  output [3:0] low,
  output [3:0] high
);

  wire and_1_out, and_2_out, clock_1_out, comparator_1_eq, counter_1_carry, counter_2_carry, or_1_out;

  Clock clock_1 (.out(clock_1_out));
  or or_1 (or_1_out, R, and_2_out);
  Counter #(.width(4), .max('h9)) counter_1 (
    .clr(or_1_out), .count(EN), .clk(clock_1_out), .carry(counter_1_carry), .Q(low));  // open: load, up, D
  Counter #(.width(4), .max('h2)) counter_2 (
    .clr(or_1_out), .count(and_1_out), .clk(clock_1_out), .carry(counter_2_carry), .Q(high));  // open: load, up, D
  and and_1 (and_1_out, counter_1_carry, EN);
  Comparator #(.width(4)) comparator_1 (.a(low), .b(4'b0100), .eq(comparator_1_eq));  // open: gt, lt
  and and_2 (and_2_out, comparator_1_eq, counter_2_carry);
endmodule

module clocker (
  input  EN,
  input  R,
  output [23:0] o
);

  wire count_to_sixty_1_c, count_to_sixty_2_c;

  count_to_sixty count_to_sixty_1 (.EN(EN), .R(R), .low(o[3:0]), .high(o[7:4]), .c(count_to_sixty_1_c));
  count_to_sixty count_to_sixty_2 (
    .EN(count_to_sixty_1_c), .R(R), .low(o[11:8]), .high(o[15:12]), .c(count_to_sixty_2_c));
  count_to_twenty count_to_twenty_1 (.EN(count_to_sixty_2_c), .R(R), .low(o[19:16]), .high(o[23:20]));
endmodule

module input_System (
  input  [5:0] b_i,
  input  nxt,
  input  R,
  output [5:0] b_o_1,
  output [5:0] b_o_2,
  output [5:0] b_o_3,
  output [5:0] b_o_4
);

  wire clock_1_out;
  wire [1:0] counter_1_q;

  Clock clock_1 (.out(clock_1_out));
  Counter #(.width(2), .max('h3)) counter_1 (
    .clr(R), .count(nxt), .clk(clock_1_out), .Q(counter_1_q));  // open: load, up, D, carry
  Demultiplexer #(.select(2), .width(6), .enable("false")) demultiplexer_1 (
    .out0(b_o_1), .out1(b_o_2), .out2(b_o_3), .out3(b_o_4), .in(b_i), .sel(counter_1_q));
endmodule

module clocker2 (
  input  EN,
  input  R,
  input  [5:0] but_i,
  output [23:0] o,
  output nxt,
  output rst
);

  wire clock_1_out, or_2_out, out_1, out_2, out_4, out_5, out_6, out_7;

  Clock clock_1 (.out(clock_1_out));
  Counter #(.width(4), .max('hf)) counter_1 (
    .clr(out_1), .count(EN), .clk(clock_1_out), .Q(o[3:0]));  // open: load, up, D, carry
  Counter #(.width(4), .max('hf)) counter_2 (.clr(out_2), .clk(out_1), .Q(o[7:4]));  // open: load, up, count, D, carry
  Counter #(.width(4), .max('hf)) counter_3 (.clr(out_4), .clk(out_2), .Q(o[11:8]));  // open: load, up, count, D, carry
  Counter #(.width(4), .max('hf)) counter_4 (
    .clr(out_5), .clk(out_4), .Q(o[15:12]));  // open: load, up, count, D, carry
  and and_1 (out_1, o[1], o[3]);
  and and_2 (out_2, o[5], o[6]);
  and and_3 (out_4, o[11], o[9]);
  or or_1 (nxt, but_i[2], but_i[3]);
  and and_4 (out_5, o[14], o[13]);
  Counter #(.width(4), .max('hf)) counter_5 (.clr(R), .clk(out_6), .Q(o[23:20]));  // open: load, up, count, D, carry
  Counter #(.width(4), .max('hf)) counter_6 (
    .clr(or_2_out), .clk(out_5), .Q(o[19:16]));  // open: load, up, count, D, carry
  or or_2 (or_2_out, R, out_6);
  and and_5 (out_7, o[20], o[21]);
  and and_6 (R, o[18], o[21]);
  and and_7 (out_6, o[17], o[19]);

  assign rst = 1'b0;

  // Other names for the same wires on the sheet: reset = R
endmodule

module alarmer (
  input  EN,
  input  R,
  input  [5:0] but_i,
  input  [23:0] t,
  output [23:0] o,
  output nxt,
  output rst,
  output sound
);

  Clock clock_1 ();  // open: out
  or or_1 (nxt, but_i[2], but_i[3]);
endmodule

module chronometer (
  input  R,
  input  [5:0] b_i,
  output [23:0] o,
  output nxt,
  output rst
);

  wire and_1_out, B, C, chron_div_1_out_1, clock_1_out, count_to_sixty_1_c, count_to_ten_1_c,
       count_to_ten_2_c, d_ff_1_q, or_1_out, or_2_out, start;

  chron_div chron_div_1 (.out_1(chron_div_1_out_1));
  or or_1 (or_1_out, R, or_2_out);
  or or_2 (or_2_out, b_i[0], b_i[1]);
  or or_3 (B, b_i[2], b_i[3]);
  or or_4 (C, b_i[4], b_i[5]);
  and and_1 (and_1_out, start, chron_div_1_out_1);
  count_to_ten count_to_ten_1 (.EN(and_1_out), .R(or_1_out), .o(o[3:0]), .c(count_to_ten_1_c));
  count_to_ten count_to_ten_2 (.EN(count_to_ten_1_c), .R(or_1_out), .o(o[7:4]), .c(count_to_ten_2_c));
  count_to_sixty count_to_sixty_1 (
    .EN(count_to_ten_2_c), .R(or_1_out), .low(o[11:8]), .high(o[15:12]), .c(count_to_sixty_1_c));
  count_to_sixty count_to_sixty_2 (.EN(count_to_sixty_1_c), .R(or_1_out), .low(o[19:16]), .high(o[23:20]));  // open: c
  T_Flip_Flop t_ff_1 (.T(C), .clk(clock_1_out), .Q(start));  // open: Qn, reset, preset
  Clock clock_1 (.out(clock_1_out));
  D_Flip_Flop d_ff_1 (.Q(d_ff_1_q), .preset(C), .reset(R));  // open: D, clk, Qn
  and and_2 (nxt, B, ~d_ff_1_q);  // AND_Gate
  and and_3 (rst, d_ff_1_q, B);

  // Other names for the same wires on the sheet: rst_t = R

  // Notes on the sheet:
  //   précision au centieme
endmodule

module count_to_ten (
  input  EN,
  input  R,
  output [3:0] o,
  output c
);

  wire clock_1_out, counter_1_carry;

  Clock clock_1 (.out(clock_1_out));
  Counter #(.width(4), .max('h9)) counter_1 (
    .clr(R), .count(EN), .clk(clock_1_out), .carry(counter_1_carry), .Q(o));  // open: load, up, D
  and and_1 (c, counter_1_carry, EN);
endmodule

module time_div (
  output out_1
);

  wire clock_1_out;

  Clock clock_1 (.out(clock_1_out));
  Counter #(.width(6), .max('h3f)) counter_1 (
    .count(1'b1), .clk(clock_1_out), .carry(out_1));  // open: clr, load, up, D, Q
endmodule

module chron_div (
  output out_1
);

  Clock clock_1 (.out(out_1));
endmodule
