// Logisim project additionner_syslog.circ as structural Verilog
module bit_counter (
  input  In3,
  input  In4
);

  wire [1:0] clock_1_out;

  Clock clock_1 (.out(clock_1_out[0]));
  Clock clock_2 (.out(clock_1_out[1]));
  Hex_Digit_Display hex_digit_display_1 (.value({In4, In3, clock_1_out}));  // open: dp
endmodule

module one_digit_display (
);

  wire clock_1_out, or_1_out, out_1, out_2, out_4, out_5, out_6, out_7, reset;
  wire [3:0] counter_1_q, counter_2_q, counter_3_q, counter_4_q, counter_5_q, counter_6_q;

  Clock clock_1 (.out(clock_1_out));
  Counter #(.width(4), .max('hf)) counter_1 (
    .clr(out_1), .clk(clock_1_out), .Q(counter_1_q));  // open: load, up, count, D, carry
  Counter #(.width(4), .max('hf)) counter_2 (
    .clr(out_2), .clk(out_1), .Q(counter_2_q));  // open: load, up, count, D, carry
  Counter #(.width(4), .max('hf)) counter_3 (
    .clr(out_4), .clk(out_2), .Q(counter_3_q));  // open: load, up, count, D, carry
  Counter #(.width(4), .max('hf)) counter_4 (
    .clr(out_5), .clk(out_4), .Q(counter_4_q));  // open: load, up, count, D, carry
  and and_1 (out_1, counter_1_q[1], counter_1_q[3]);
  and and_2 (out_2, counter_2_q[1], counter_2_q[2]);
  and and_3 (out_4, counter_3_q[3], counter_3_q[1]);
  and and_4 (out_5, counter_4_q[2], counter_4_q[1]);
  Counter #(.width(4), .max('hf)) counter_5 (
    .clr(reset), .clk(out_6), .Q(counter_5_q));  // open: load, up, count, D, carry
  Counter #(.width(4), .max('hf)) counter_6 (
    .clr(or_1_out), .clk(out_5), .Q(counter_6_q));  // open: load, up, count, D, carry
  or or_1 (or_1_out, reset, out_6);
  Hex_Digit_Display hex_digit_display_1 (.value(counter_5_q));  // open: dp
  Hex_Digit_Display hex_digit_display_2 (.value(counter_6_q));  // open: dp
  Hex_Digit_Display hex_digit_display_3 (.value(counter_4_q));  // open: dp
  Hex_Digit_Display hex_digit_display_4 (.value(counter_3_q));  // open: dp
  Hex_Digit_Display hex_digit_display_5 (.value(counter_1_q));  // open: dp
  Hex_Digit_Display hex_digit_display_6 (.value(counter_2_q));  // open: dp
  and and_5 (out_7, counter_5_q[0], counter_5_q[1]);
  and and_6 (reset, counter_6_q[2], counter_5_q[1]);
  and and_7 (out_6, counter_6_q[1], counter_6_q[3]);
endmodule

module divide_by_2 (
  input  clock_input,
  output ou1
);

  wire d_ff_1_q, d_ff_1_qn;

  D_Flip_Flop d_ff_1 (.D(d_ff_1_qn), .clk(clock_input), .Q(d_ff_1_q), .Qn(d_ff_1_qn));  // open: preset, reset
  not not_1 (ou1, d_ff_1_q);
endmodule

module divide_by_4 (
  input  clock_input,
  output ou2
);

  wire d_ff_1_q, d_ff_1_qn, d_ff_2_qn;

  D_Flip_Flop d_ff_1 (.D(d_ff_1_qn), .clk(clock_input), .Q(d_ff_1_q), .Qn(d_ff_1_qn));  // open: preset, reset
  D_Flip_Flop d_ff_2 (.D(d_ff_2_qn), .clk(d_ff_1_q), .Q(ou2), .Qn(d_ff_2_qn));  // open: preset, reset
endmodule

module divide_by_8 (
  input  clock_input,
  output ou3
);

  wire d_ff_1_q, d_ff_1_qn, d_ff_2_q, d_ff_2_qn, d_ff_3_q, d_ff_3_qn;

  D_Flip_Flop d_ff_1 (.D(d_ff_1_qn), .clk(clock_input), .Q(d_ff_1_q), .Qn(d_ff_1_qn));  // open: preset, reset
  D_Flip_Flop d_ff_2 (.D(d_ff_2_qn), .clk(d_ff_1_q), .Q(d_ff_2_q), .Qn(d_ff_2_qn));  // open: preset, reset
  D_Flip_Flop d_ff_3 (.D(d_ff_3_qn), .clk(d_ff_2_q), .Q(d_ff_3_q), .Qn(d_ff_3_qn));  // open: preset, reset
  not not_1 (ou3, d_ff_3_q);
endmodule

module additionner_0_9 (
  input  CLK_input,
  output c_out,
  output [3:0] out_3
);

  wire and_1_out, and_2_out, d_ff_1_qn, j_k_ff_1_q, j_k_ff_2_q, j_k_ff_3_q, not_1_out, not_2_out, not_3_out,
       not_4_out, undriven;

  J_K_Flip_Flop j_k_ff_1 (
    .J(1'b1), .K(1'b1), .clk(CLK_input), .Q(j_k_ff_1_q), .Qn(out_3[0]), .preset(and_1_out));  // open: reset
  J_K_Flip_Flop j_k_ff_2 (
    .J(1'b1), .K(1'b1), .clk(j_k_ff_1_q), .Q(j_k_ff_2_q), .Qn(out_3[1]), .preset(and_1_out), .reset(undriven));
  J_K_Flip_Flop j_k_ff_3 (
    .J(1'b1), .K(1'b1), .clk(j_k_ff_2_q), .Q(j_k_ff_3_q), .Qn(out_3[2]), .preset(and_1_out));  // open: reset
  not not_1 (not_1_out, j_k_ff_2_q);
  J_K_Flip_Flop j_k_ff_4 (.J(1'b1), .K(1'b1), .clk(j_k_ff_3_q), .Qn(out_3[3]), .preset(and_1_out));  // open: Q, reset
  and and_1 (and_1_out, not_1_out, out_3[3]);
  not not_2 (not_2_out, out_3[1]);
  not not_3 (not_3_out, out_3[2]);
  not not_4 (not_4_out, out_3[3]);
  D_Flip_Flop d_ff_1 (.D(d_ff_1_qn), .clk(and_1_out), .Q(c_out), .Qn(d_ff_1_qn), .reset(and_2_out));  // open: preset
  and and_2 (and_2_out, out_3[0], not_2_out, not_3_out, not_4_out);
endmodule

module additionneur_0_5 (
  input  CLK_input,
  output c_out,
  output [3:0] out_3
);

  wire and_1_out, and_2_out, d_ff_1_qn, j_k_ff_1_q, j_k_ff_2_q, not_2_out, not_3_out, undriven;

  J_K_Flip_Flop j_k_ff_1 (
    .J(1'b1), .K(1'b1), .clk(CLK_input), .Q(j_k_ff_1_q), .Qn(out_3[0]), .preset(and_1_out));  // open: reset
  J_K_Flip_Flop j_k_ff_2 (
    .J(1'b1), .K(1'b1), .clk(j_k_ff_1_q), .Q(j_k_ff_2_q), .Qn(out_3[1]), .preset(and_1_out), .reset(undriven));
  J_K_Flip_Flop j_k_ff_3 (.J(1'b1), .K(1'b1), .clk(j_k_ff_2_q), .Qn(out_3[2]), .preset(and_1_out));  // open: Q, reset
  not not_1 (out_3[3], 1'b1);
  and and_1 (and_1_out, out_3[1], out_3[2]);
  not not_2 (not_2_out, out_3[1]);
  not not_3 (not_3_out, out_3[2]);
  D_Flip_Flop d_ff_1 (.D(d_ff_1_qn), .clk(and_1_out), .Q(c_out), .Qn(d_ff_1_qn), .reset(and_2_out));  // open: preset
  and and_2 (and_2_out, out_3[0], not_2_out, not_3_out);
endmodule

module additionneur_0_2 (
  input  CLK_input,
  output out_2,
  output [3:0] out_3
);

  wire and_1_out, and_2_out, d_ff_1_qn, j_k_ff_1_q, not_2_out, not_3_out, undriven;

  J_K_Flip_Flop j_k_ff_1 (
    .J(1'b1), .K(1'b1), .clk(CLK_input), .Q(j_k_ff_1_q), .Qn(out_3[0]), .preset(and_1_out));  // open: reset
  J_K_Flip_Flop j_k_ff_2 (
    .J(1'b1), .K(1'b1), .clk(j_k_ff_1_q), .Qn(out_3[1]), .preset(and_1_out), .reset(undriven));  // open: Q
  not not_1 (out_3[3], 1'b1);
  and and_1 (and_1_out, out_3[0], out_3[1]);
  not not_2 (not_2_out, out_3[1]);
  not not_3 (not_3_out, out_3[1]);
  D_Flip_Flop d_ff_1 (.D(d_ff_1_qn), .clk(and_1_out), .Q(out_2), .Qn(d_ff_1_qn), .reset(and_2_out));  // open: preset
  and and_2 (and_2_out, out_3[0], not_2_out, not_3_out);

  assign out_3[2] = out_3[3];
endmodule

module additionner_0_4 (
  input  in_1,
  input  R,
  output out_3,
  output [3:0] out_4
);

  wire and_1_out, and_2_out, d_ff_1_qn, j_k_ff_1_q, j_k_ff_2_q, not_2_out, not_3_out, not_4_out, or_1_out;

  J_K_Flip_Flop j_k_ff_1 (.J(1'b1), .K(1'b1), .clk(in_1), .Q(j_k_ff_1_q), .Qn(out_4[0]), .preset(and_1_out), .reset(R));
  J_K_Flip_Flop j_k_ff_2 (
    .J(1'b1), .K(1'b1), .clk(j_k_ff_1_q), .Q(j_k_ff_2_q), .Qn(out_4[1]), .preset(and_1_out), .reset(R));
  J_K_Flip_Flop j_k_ff_3 (
    .J(1'b1), .K(1'b1), .clk(j_k_ff_2_q), .Qn(out_4[2]), .preset(and_1_out), .reset(R));  // open: Q
  not not_1 (out_4[3], 1'b1);
  not not_2 (not_2_out, out_4[1]);
  not not_3 (not_3_out, out_4[0]);
  and and_1 (and_1_out, not_2_out, not_3_out, out_4[2]);
  not not_4 (not_4_out, out_4[1]);
  D_Flip_Flop d_ff_1 (.D(d_ff_1_qn), .clk(and_1_out), .Q(out_3), .Qn(d_ff_1_qn), .reset(or_1_out));  // open: preset
  or or_1 (or_1_out, and_2_out, R);
  and and_2 (and_2_out, out_4[0], not_4_out, out_4[2]);

  // Notes on the sheet:
  //   reset
endmodule

module format_alterner_24 (
  input  in_1,
  output out_2
);

  wire and_1_out, d_ff_1_q, d_ff_2_q, d_ff_2_qn, not_1_out;

  D_Flip_Flop d_ff_1 (.D(d_ff_2_qn), .clk(in_1), .Q(d_ff_1_q), .reset(and_1_out));  // open: Qn, preset
  not not_1 (not_1_out, d_ff_1_q);
  and and_1 (and_1_out, not_1_out, d_ff_2_q);
  D_Flip_Flop d_ff_2 (.D(d_ff_1_q), .clk(in_1), .Q(d_ff_2_q), .Qn(d_ff_2_qn), .reset(and_1_out));  // open: preset
  xor xor_1 (out_2, d_ff_1_q, d_ff_2_q);
endmodule
