// Logisim project piloufasV2.circ as structural Verilog: 23 circuits, main circuit main
module main (
  output ringer
);

  wire A_out, alarmer_1_mode, B_out, clock_1_out, clock_2_out, clock_3_out, clock_4_out, converter_mod_one,
       converter_mod_three, converter_mod_two, converter_mod_zero, d_1, d_2, d_ff_3_q, dayTogg,
       DipSwitch_1_sw2, hour_high_bot, hour_high_cen, hour_high_l_b, hour_high_l_h, hour_high_r_b,
       hour_high_r_h, hour_high_top, hour_low_bot, hour_low_cen, hour_low_l_b, hour_low_l_h, hour_low_r_b,
       hour_low_r_h, hour_low_top, min_high_bot, min_high_cen, min_high_l_b, min_high_l_h, min_high_r_b,
       min_high_r_h, min_high_top, min_low_bot, min_low_cen, min_low_l_b, min_low_l_h, min_low_r_b,
       min_low_r_h, min_low_top, not_1_out, not_2_out, nxt, nxt_ala, nxt_chr, nxt_clk, nxt_tim, or_1_out,
       or_2_out, or_3_out, R, r_alar, r_chron, r_tim, rst, second_high_bot, second_high_cen, second_high_l_b,
       second_high_l_h, second_high_r_b, second_high_r_h, second_high_top, second_low_bot, second_low_cen,
       second_low_l_b, second_low_l_h, second_low_r_b, second_low_r_h, second_low_top,
       stabilisation_input_a_l, stabilisation_input_a_s, stabilisation_input_b_l, stabilisation_input_b_s,
       stabilisation_input_c;
  wire [1:0] mode;
  wire [3:0] d1, d2;
  wire [4:0] b_ala, b_chr, b_clk, b_tim, but_array;
  wire [11:8] day_dat;
  wire [23:0] d_alar, d_chr, d_clk, d_tim, display_1_data;

  Clock sysclk ();  // open: out
  Button A (.out(A_out));
  Button B (.out(B_out));
  DipSwitch DipSwitch_1 (.sw1(rst), .sw2(DipSwitch_1_sw2));  // open: sw3, sw4, sw5, sw6, sw7, sw8
  stabilisation stabilisation_input (
    .A(A_out), .B(B_out), .A_L(stabilisation_input_a_l), .A_S(stabilisation_input_a_s),
    .C(stabilisation_input_c), .B_L(stabilisation_input_b_l), .B_S(stabilisation_input_b_s));
  D_Flip_Flop d_ff_1 (.D(or_1_out), .clk(clock_1_out), .Q(nxt));  // open: Qn, preset, reset
  or or_1 (or_1_out, nxt_clk, nxt_ala, nxt_chr, nxt_tim);
  Clock clock_1 (.out(clock_1_out));
  D_Flip_Flop d_ff_2 (.D(or_2_out), .clk(clock_2_out), .Q(R));  // open: Qn, preset, reset
  or or_2 (or_2_out, r_chron, r_alar, r_tim);
  Clock clock_2 (.out(clock_2_out));
  LED mod1 (.in(converter_mod_zero));
  mode_conv converter_mod (
    .i(mode), .zero(converter_mod_zero), .one(converter_mod_one), .two(converter_mod_two),
    .three(converter_mod_three));
  LED mod2 (.in(converter_mod_one));
  LED mod3 (.in(converter_mod_two));
  LED mod4 (.in(converter_mod_three));
  dispatcher dispatcher_1 (
    .but_in(but_array), .nxt(nxt), .R(R), .to_clock(b_clk), .to_alarm(b_ala), .to_chron(b_chr),
    .to_timer(b_tim), .mode(mode));
  button_array convert_to_array (
    .A_L(stabilisation_input_a_l), .A_S(stabilisation_input_a_s), .C(stabilisation_input_c),
    .B_L(stabilisation_input_b_l), .B_S(stabilisation_input_b_s), .o(but_array));
  LED A_lg (.in(but_array[0]));
  LED A_st (.in(but_array[1]));
  LED C (.in(but_array[2]));
  LED B_lg (.in(but_array[3]));
  LED B_st (.in(but_array[4]));
  D_Flip_Flop d_ff_3 (.D(or_3_out), .clk(clock_3_out), .Q(d_ff_3_q), .reset(DipSwitch_1_sw2));  // open: Qn, preset
  or or_3 (or_3_out, d_2, d_1);
  Clock clock_3 (.out(clock_3_out));
  timer timer_1 (.b_in(b_tim), .data(d_tim), .nxt(nxt_tim), .R(r_tim), .alarm(d_2));
  T_Flip_Flop t_ff_1 (.T(d_ff_3_q), .clk(clock_4_out), .Q(ringer), .reset(DipSwitch_1_sw2));  // open: Qn, preset
  Clock clock_4 (.out(clock_4_out));
  hour_date hour_date_1 (
    .b_in(b_clk), .R(rst), .d_out(d_clk), .day_out({day_dat, d2, d1}), .nxt(nxt_clk), .day(dayTogg));
  alarmer alarmer_1 (
    .b_in(b_ala), .t(d_clk), .d_out(d_alar), .nxt(nxt_ala), .R(r_alar), .mode(alarmer_1_mode), .alarm(d_1));
  chron chron_1 (.but_i(b_chr), .res(rst), .data(d_chr), .nxt(nxt_chr), .R(r_chron));
  LED alarm_led (.in(alarmer_1_mode));
  display display_1 (
    .from_clock(d_clk), .from_alarm(d_alar), .from_chron(d_chr), .from_timer(d_tim), .nxt(nxt), .R(R),
    .data(display_1_data));
  seven second_high (
    .Input_bus_1(display_1_data[7:4]), .d_day(day_dat), .day(dayTogg), .monthType(2'b11),
    .cen(second_high_cen), .l_h(second_high_l_h), .top(second_high_top), .r_h(second_high_r_h),
    .l_b(second_high_l_b), .bot(second_high_bot), .r_b(second_high_r_b));
  seven min_low (
    .Input_bus_1(display_1_data[11:8]), .d_day(day_dat), .day(dayTogg), .monthType(2'b10), .cen(min_low_cen),
    .l_h(min_low_l_h), .top(min_low_top), .r_h(min_low_r_h), .l_b(min_low_l_b), .bot(min_low_bot),
    .r_b(min_low_r_b));
  seven min_high (
    .Input_bus_1(display_1_data[15:12]), .d_day(day_dat), .day(dayTogg), .monthType(2'b01),
    .cen(min_high_cen), .l_h(min_high_l_h), .top(min_high_top), .r_h(min_high_r_h), .l_b(min_high_l_b),
    .bot(min_high_bot), .r_b(min_high_r_b));
  seven hour_low (
    .Input_bus_1(display_1_data[19:16]), .d_day(d2), .day(dayTogg), .monthType(2'b00), .cen(hour_low_cen),
    .l_h(hour_low_l_h), .top(hour_low_top), .r_h(hour_low_r_h), .l_b(hour_low_l_b), .bot(hour_low_bot),
    .r_b(hour_low_r_b));
  seven hour_high (
    .Input_bus_1(display_1_data[23:20]), .d_day(d1), .day(dayTogg), .monthType(2'b00), .cen(hour_high_cen),
    .l_h(hour_high_l_h), .top(hour_high_top), .r_h(hour_high_r_h), .l_b(hour_high_l_b), .bot(hour_high_bot),
    .r_b(hour_high_r_b));
  seven second_low (
    .Input_bus_1(display_1_data[3:0]), .d_day(4'b1110), .day(dayTogg), .monthType(2'b00),
    .cen(second_low_cen), .l_h(second_low_l_h), .top(second_low_top), .r_h(second_low_r_h),
    .l_b(second_low_l_b), .bot(second_low_bot), .r_b(second_low_r_b));
  _7_Segment_Display L_7_Segment_Display_1 (
    .g(second_low_cen), .f(second_low_l_h), .a(second_low_top), .b(second_low_r_h), .e(second_low_l_b),
    .d(second_low_bot), .c(second_low_r_b), .dp(1'b0));
  _7_Segment_Display L_7_Segment_Display_2 (
    .g(second_high_cen), .f(second_high_l_h), .a(second_high_top), .b(second_high_r_h), .e(second_high_l_b),
    .d(second_high_bot), .c(second_high_r_b), .dp(1'b0));
  _7_Segment_Display L_7_Segment_Display_3 (
    .g(min_low_cen), .f(min_low_l_h), .a(min_low_top), .b(min_low_r_h), .e(min_low_l_b), .d(min_low_bot),
    .c(min_low_r_b), .dp(not_1_out));
  not not_1 (not_1_out, 1'b0);
  _7_Segment_Display L_7_Segment_Display_4 (
    .g(min_high_cen), .f(min_high_l_h), .a(min_high_top), .b(min_high_r_h), .e(min_high_l_b),
    .d(min_high_bot), .c(min_high_r_b), .dp(1'b0));
  _7_Segment_Display L_7_Segment_Display_5 (
    .g(hour_low_cen), .f(hour_low_l_h), .a(hour_low_top), .b(hour_low_r_h), .e(hour_low_l_b),
    .d(hour_low_bot), .c(hour_low_r_b), .dp(not_2_out));
  not not_2 (not_2_out, 1'b0);
  _7_Segment_Display L_7_Segment_Display_6 (
    .g(hour_high_cen), .f(hour_high_l_h), .a(hour_high_top), .b(hour_high_r_h), .e(hour_high_l_b),
    .d(hour_high_bot), .c(hour_high_r_b), .dp(1'b0));

  // Other names for the same wires on the sheet: day_dat[7:0] = {d2, d1}; m1[3:0] = day_dat
endmodule

module dispatcher (
  input  [4:0] but_in,
  input  nxt,
  input  R,
  output [4:0] to_clock,
  output [4:0] to_alarm,
  output [4:0] to_chron,
  output [4:0] to_timer,
  output [1:0] mode
);

  wire and_1_out, and_2_out, clock_1_out, clock_2_out, d_ff_1_q, d_ff_1_qn;

  Clock clock_1 (.out(clock_1_out));
  D_Flip_Flop d_ff_1 (.D(and_1_out), .clk(clock_1_out), .Q(d_ff_1_q), .Qn(d_ff_1_qn));  // open: preset, reset
  and and_1 (and_1_out, d_ff_1_qn, nxt);
  T_Flip_Flop t_ff_1 (.T(d_ff_1_q), .clk(clock_2_out), .Q(mode[0]), .reset(R));  // open: Qn, preset
  Clock clock_2 (.out(clock_2_out));
  and and_2 (and_2_out, d_ff_1_q, mode[0]);
  T_Flip_Flop t_ff_2 (.T(and_2_out), .clk(clock_2_out), .Q(mode[1]), .reset(R));  // open: Qn, preset
  Demultiplexer #(.select(2), .width(5), .enable("false")) demultiplexer_1 (
    .out0(to_clock), .out1(to_alarm), .out2(to_chron), .out3(to_timer), .in(but_in), .sel(mode));
endmodule

module display (
  input  [23:0] from_clock,
  input  [23:0] from_alarm,
  input  [23:0] from_chron,
  input  [23:0] from_timer,
  input  nxt,
  input  R,
  output [23:0] data
);

  wire and_1_out, clock_1_out;
  wire [1:0] t_ff_1_q;

  T_Flip_Flop t_ff_1 (.T(nxt), .clk(clock_1_out), .Q(t_ff_1_q[0]), .reset(R));  // open: Qn, preset
  Clock clock_1 (.out(clock_1_out));
  T_Flip_Flop t_ff_2 (.T(and_1_out), .clk(clock_1_out), .Q(t_ff_1_q[1]), .reset(R));  // open: Qn, preset
  and and_1 (and_1_out, nxt, t_ff_1_q[0]);
  Multiplexer #(.select(2), .width(24), .enable("false")) multiplexer_1 (
    .in0(from_clock), .in1(from_alarm), .in2(from_chron), .in3(from_timer), .out(data), .sel(t_ff_1_q));
endmodule

module hour_date (
  input  [4:0] b_in,
  input  R,
  output [23:0] d_out,
  output [11:0] day_out,
  output nxt,
  output day
);

  wire clock_1_out;

  // clocker clocker_1: pin names not known; wires that end beside it: b_in[0], b_in[1], b_in[2], b_in[2], R, d_out[23:20], d_out[19:16], d_out[15:12], d_out[11:8], d_out[7:4], d_out[3:0], day_out[3:0], day_out[7:4], day_out[11:8]
  T_Flip_Flop t_ff_1 (.T(b_in[3]), .clk(clock_1_out), .Q(day), .reset(R));  // open: Qn, preset
  Clock clock_1 (.out(clock_1_out));

  assign nxt = b_in[4];

  // Other names for the same wires on the sheet: A_lg = b_in[0]; A_st = b_in[1]; C = b_in[2]; B_lg = b_in[3];
  //   B = b_in[4]
endmodule

module chron (
  input  [4:0] but_i,
  input  res,
  output [23:0] data,
  output nxt,
  output R
);

  wire A, B, C, clock_1_out, clock_2_out, clock_3_out, count5_o, count_10_1_c_out, count_512_1_o, d_ff_1_q,
       d_ff_2_q, min_low_c_out, or_3_out, or_5_out, or_6_out, or_7_out, sec_high_c_out, sec_low_c_out, START;

  or or_1 (A, but_i[0], but_i[1]);
  or or_2 (B, but_i[3], but_i[4]);
  count_5 count5 (.EN(START), .R(C), .o(count5_o));
  or or_3 (or_3_out, C, sec_low_c_out);
  count_512 count_512_1 (.EN(START), .R(C), .o(count_512_1_o));
  or or_4 (C, but_i[2], res);
  count_10 count_10_1 (.EN(count5_o), .R(or_3_out), .data_o(data[3:0]), .c_out(count_10_1_c_out));
  count_10 count_10_2 (.EN(count_10_1_c_out), .R(or_3_out), .data_o(data[7:4]));  // open: c_out
  count_10 sec_low (.EN(count_512_1_o), .R(C), .data_o(data[11:8]), .c_out(sec_low_c_out));
  count_6 sec_high (.EN(sec_low_c_out), .R(C), .data_o(data[15:12]), .c_out(sec_high_c_out));
  count_10 min_low (.EN(sec_high_c_out), .R(C), .data_o(data[19:16]), .c_out(min_low_c_out));
  count_6 min_high (.EN(min_low_c_out), .R(C), .data_o(data[23:20]));  // open: c_out
  or or_5 (or_5_out, A, C);
  Clock clock_1 (.out(clock_1_out));
  D_Flip_Flop d_ff_1 (.D(or_6_out), .clk(clock_2_out), .Q(d_ff_1_q), .reset(or_7_out));  // open: Qn, preset
  or or_6 (or_6_out, d_ff_1_q, or_5_out);
  Clock clock_2 (.out(clock_2_out));
  or or_7 (or_7_out, res, d_ff_2_q);
  T_Flip_Flop t_ff_1 (.T(A), .clk(clock_1_out), .Q(START), .reset(C));  // open: Qn, preset
  D_Flip_Flop d_ff_2 (.D(B), .clk(clock_3_out), .Q(d_ff_2_q));  // open: Qn, preset, reset
  Clock clock_3 (.out(clock_3_out));
  and and_1 (nxt, B, ~d_ff_1_q);  // AND_Gate
  and and_2 (R, d_ff_1_q, B);
endmodule

module alarmer (
  input  [4:0] b_in,
  input  [23:0] t,
  output [23:0] d_out,
  output nxt,
  output R,
  output mode,
  output alarm
);

  wire and_1_out, and_8_out, and_9_out, and_10_out, and_11_out, and_12_out, and_13_out,
       bidirectionnal_6_2_carry, c_1, c_2, c_3, c_4, c_5, c_6, cli, clock_1_out, clock_2_out, clock_3_out,
       clock_4_out, clock_5_out, comparer_1_same, count_6_1_c_out, count_100_1_o, d_ff_2_q, d_ff_3_q,
       demultiplexer_1_out0, demultiplexer_1_out1, demultiplexer_1_out2, demultiplexer_1_out3,
       demultiplexer_1_out4, demultiplexer_1_out5, not_1_out, or_1_out, or_2_out, or_3_out, res, set_end,
       set_mode;
  wire [3:0] bidirectionnal_6_1_data, bidirectionnal_6_2_data, bidirectionnal_10_1_data,
       bidirectionnal_10_2_data, bidirectionnal_10_3_data, bidirectionnal_10_4_data, count_6_1_data_o;

  and and_1 (and_1_out, set_mode, b_in[1]);
  Demultiplexer #(.select(3), .enable("false")) demultiplexer_1 (
    .out0(demultiplexer_1_out0), .out1(demultiplexer_1_out1), .out2(demultiplexer_1_out2),
    .out3(demultiplexer_1_out3), .out4(demultiplexer_1_out4), .out5(demultiplexer_1_out5), .in(and_1_out),
    .sel(count_6_1_data_o[2:0]));  // open: out6, out7
  count_6 count_6_1 (.EN(b_in[2]), .R(set_end), .data_o(count_6_1_data_o), .c_out(count_6_1_c_out));
  D_Flip_Flop d_ff_1 (.D(count_6_1_c_out), .clk(clock_1_out), .Q(set_end));  // open: Qn, preset, reset
  Clock clock_1 (.out(clock_1_out));
  and and_2 (c_1, ~count_6_1_data_o[0], ~count_6_1_data_o[1], ~count_6_1_data_o[2]);  // AND_Gate
  and and_3 (c_2, count_6_1_data_o[0], ~count_6_1_data_o[1], ~count_6_1_data_o[2]);  // AND_Gate
  and and_4 (c_3, ~count_6_1_data_o[0], count_6_1_data_o[1], ~count_6_1_data_o[2]);  // AND_Gate
  and and_5 (c_4, count_6_1_data_o[0], count_6_1_data_o[1], ~count_6_1_data_o[2]);  // AND_Gate
  and and_6 (c_5, ~count_6_1_data_o[0], ~count_6_1_data_o[1], count_6_1_data_o[2]);  // AND_Gate
  and and_7 (c_6, count_6_1_data_o[0], ~count_6_1_data_o[1], count_6_1_data_o[2]);  // AND_Gate
  not not_1 (not_1_out, set_mode);
  T_Flip_Flop t_ff_1 (.T(count_100_1_o), .clk(clock_2_out), .Q(cli), .reset(not_1_out));  // open: Qn, preset
  count_100 count_100_1 (.EN(set_mode), .R(not_1_out), .o(count_100_1_o));
  Clock clock_2 (.out(clock_2_out));
  bidirectionnal_10 bidirectionnal_10_1 (
    .EN(demultiplexer_1_out0), .UP(set_mode), .R(res), .data(bidirectionnal_10_1_data));  // open: carry
  bidirectionnal_6 bidirectionnal_6_1 (
    .EN(demultiplexer_1_out1), .UP(set_mode), .R(res), .data(bidirectionnal_6_1_data));  // open: carry
  bidirectionnal_10 bidirectionnal_10_2 (
    .EN(demultiplexer_1_out2), .UP(set_mode), .R(res), .data(bidirectionnal_10_2_data));  // open: carry
  bidirectionnal_6 bidirectionnal_6_2 (
    .EN(demultiplexer_1_out3), .UP(set_mode), .R(res), .data(bidirectionnal_6_2_data),
    .carry(bidirectionnal_6_2_carry));
  bidirectionnal_10 bidirectionnal_10_3 (
    .EN(demultiplexer_1_out4), .UP(set_mode), .R(res), .data(bidirectionnal_10_3_data));  // open: carry
  bidirectionnal_10 bidirectionnal_10_4 (
    .EN(demultiplexer_1_out5), .UP(set_mode), .R(res), .data(bidirectionnal_10_4_data));  // open: carry
  Multiplexer #(.width(4), .enable("false")) multiplexer_1 (
    .in0(bidirectionnal_10_1_data), .in1(4'b1110), .out(d_out[3:0]), .sel(and_8_out));
  and and_8 (and_8_out, cli, c_1);
  and and_9 (and_9_out, cli, c_2);
  Multiplexer #(.width(4), .enable("false")) multiplexer_2 (
    .in0(bidirectionnal_10_2_data), .in1(4'b1110), .out(d_out[11:8]), .sel(and_10_out));
  and and_10 (and_10_out, cli, c_3);
  Multiplexer #(.width(4), .enable("false")) multiplexer_3 (
    .in0(bidirectionnal_6_2_data), .in1(4'b1110), .out(d_out[15:12]), .sel(and_11_out));
  and and_11 (and_11_out, cli, c_4);
  Multiplexer #(.width(4), .enable("false")) multiplexer_4 (
    .in0(bidirectionnal_10_3_data), .in1(4'b1110), .out(d_out[19:16]), .sel(and_12_out));
  and and_12 (and_12_out, cli, c_5);
  Multiplexer #(.width(4), .enable("false")) multiplexer_5 (
    .in0(bidirectionnal_10_4_data), .in1(4'b1110), .out(d_out[23:20]), .sel(and_13_out));
  and and_13 (and_13_out, cli, c_6);
  Multiplexer #(.width(4), .enable("false")) multiplexer_6 (
    .in0(bidirectionnal_6_1_data), .in1(4'b1110), .out(d_out[7:4]), .sel(and_9_out));
  and and_14 (res, ~set_mode, ~set_end, b_in[2]);  // AND_Gate
  comparer comparer_1 (.a(d_out), .b(t), .same(comparer_1_same));
  Clock clock_3 (.out(clock_3_out));
  or or_1 (or_1_out, b_in[1], b_in[0], b_in[2]);
  T_Flip_Flop t_ff_2 (.T(b_in[0]), .clk(clock_3_out), .Qn(set_mode), .reset(set_end));  // open: Q, preset
  D_Flip_Flop d_ff_2 (.D(or_2_out), .clk(clock_4_out), .Q(d_ff_2_q), .reset(d_ff_3_q));  // open: Qn, preset
  or or_2 (or_2_out, d_ff_2_q, or_1_out);
  Clock clock_4 (.out(clock_4_out));
  and and_15 (alarm, ~set_mode, comparer_1_same);  // AND_Gate
  not not_2 (mode, set_mode);
  or or_3 (or_3_out, b_in[4], b_in[3]);
  D_Flip_Flop d_ff_3 (.D(or_3_out), .clk(clock_5_out), .Q(d_ff_3_q));  // open: Qn, preset, reset
  Clock clock_5 (.out(clock_5_out));
  and and_16 (nxt, or_3_out, ~d_ff_2_q);  // AND_Gate
  and and_17 (R, d_ff_2_q, or_3_out);

  // Other names for the same wires on the sheet: A_lg = b_in[0]; A_st = b_in[1]; C = b_in[2]; B_lg = b_in[3];
  //   B_st = b_in[4]; dring = alarm; ti[23:0] = t
endmodule

module timer (
  input  [4:0] b_in,
  output [23:0] data,
  output nxt,
  output R,
  output alarm
);

  wire and_1_out, and_8_out, and_9_out, and_10_out, and_11_out, and_12_out, and_13_out, and_14_out,
       and_15_out, and_16_out, and_17_out, and_18_out, and_20_out, and_21_out, c_1, c_2, c_3, c_4, c_5, c_6,
       cli, clock_1_out, clock_2_out, clock_3_out, clock_4_out, clock_5_out, clock_6_out, clock_7_out,
       clock_8_out, comparer_1_same, count_6_1_c_out, d_ff_2_q, d_ff_3_q, d_ff_5_q, demultiplexer_1_out0,
       demultiplexer_1_out1, demultiplexer_1_out2, demultiplexer_1_out3, demultiplexer_1_out4,
       demultiplexer_1_out5, div100_o, hour_low_carry, min_high_carry, min_low_carry, not_1_out, or_1_out,
       or_2_out, or_3_out, or_4_out, or_5_out, or_6_out, or_7_out, or_8_out, or_9_out, or_10_out, or_11_out,
       or_12_out, or_13_out, res, sec_high_carry, sec_low_carry, set_end, set_mode, START, t_ff_3_q;
  wire [3:0] count_6_1_data_o, hour_high_data, hour_low_data, min_high_data, min_low_data, sec_high_data,
       sec_low_data;

  and and_1 (and_1_out, set_mode, b_in[1]);
  Demultiplexer #(.select(3), .enable("false")) demultiplexer_1 (
    .out0(demultiplexer_1_out0), .out1(demultiplexer_1_out1), .out2(demultiplexer_1_out2),
    .out3(demultiplexer_1_out3), .out4(demultiplexer_1_out4), .out5(demultiplexer_1_out5), .in(and_1_out),
    .sel(count_6_1_data_o[2:0]));  // open: out6, out7
  count_6 count_6_1 (.EN(b_in[2]), .R(set_end), .data_o(count_6_1_data_o), .c_out(count_6_1_c_out));
  D_Flip_Flop d_ff_1 (.D(count_6_1_c_out), .clk(clock_1_out), .Q(set_end));  // open: Qn, preset, reset
  Clock clock_1 (.out(clock_1_out));
  and and_2 (c_1, ~count_6_1_data_o[0], ~count_6_1_data_o[1], ~count_6_1_data_o[2]);  // AND_Gate
  and and_3 (c_2, count_6_1_data_o[0], ~count_6_1_data_o[1], ~count_6_1_data_o[2]);  // AND_Gate
  and and_4 (c_3, ~count_6_1_data_o[0], count_6_1_data_o[1], ~count_6_1_data_o[2]);  // AND_Gate
  and and_5 (c_4, count_6_1_data_o[0], count_6_1_data_o[1], ~count_6_1_data_o[2]);  // AND_Gate
  and and_6 (c_5, ~count_6_1_data_o[0], ~count_6_1_data_o[1], count_6_1_data_o[2]);  // AND_Gate
  and and_7 (c_6, count_6_1_data_o[0], ~count_6_1_data_o[1], count_6_1_data_o[2]);  // AND_Gate
  not not_1 (not_1_out, set_mode);
  or or_1 (or_1_out, START, demultiplexer_1_out0);
  or or_2 (or_2_out, and_8_out, demultiplexer_1_out1);
  T_Flip_Flop t_ff_1 (.T(div100_o), .clk(clock_2_out), .Q(cli), .reset(not_1_out));  // open: Qn, preset
  count_100 div100 (.EN(set_mode), .R(not_1_out), .o(div100_o));
  Clock clock_2 (.out(clock_2_out));
  or or_3 (or_3_out, and_9_out, demultiplexer_1_out2);
  or or_4 (or_4_out, and_10_out, demultiplexer_1_out3);
  or or_5 (or_5_out, and_11_out, demultiplexer_1_out4);
  or or_6 (or_6_out, and_12_out, demultiplexer_1_out5);
  and and_8 (and_8_out, sec_low_carry, START);
  and and_9 (and_9_out, sec_high_carry, START);
  and and_10 (and_10_out, min_low_carry, START);
  and and_11 (and_11_out, min_high_carry, START);
  and and_12 (and_12_out, hour_low_carry, START);
  bidirectionnal_10 sec_low (.EN(or_1_out), .UP(set_mode), .R(res), .data(sec_low_data), .carry(sec_low_carry));
  bidirectionnal_6 sec_high (.EN(or_2_out), .UP(set_mode), .R(res), .data(sec_high_data), .carry(sec_high_carry));
  bidirectionnal_10 min_low (.EN(or_3_out), .UP(set_mode), .R(res), .data(min_low_data), .carry(min_low_carry));
  bidirectionnal_6 min_high (.EN(or_4_out), .UP(set_mode), .R(res), .data(min_high_data), .carry(min_high_carry));
  bidirectionnal_10 hour_low (.EN(or_5_out), .UP(set_mode), .R(res), .data(hour_low_data), .carry(hour_low_carry));
  bidirectionnal_10 hour_high (.EN(or_6_out), .UP(set_mode), .R(res), .data(hour_high_data));  // open: carry
  Multiplexer #(.width(4), .enable("false")) multiplexer_1 (
    .in0(sec_low_data), .in1(4'b1110), .out(data[3:0]), .sel(and_13_out));
  and and_13 (and_13_out, cli, c_1);
  and and_14 (and_14_out, cli, c_2);
  Multiplexer #(.width(4), .enable("false")) multiplexer_2 (
    .in0(min_low_data), .in1(4'b1110), .out(data[11:8]), .sel(and_15_out));
  and and_15 (and_15_out, cli, c_3);
  Multiplexer #(.width(4), .enable("false")) multiplexer_3 (
    .in0(min_high_data), .in1(4'b1110), .out(data[15:12]), .sel(and_16_out));
  and and_16 (and_16_out, cli, c_4);
  Multiplexer #(.width(4), .enable("false")) multiplexer_4 (
    .in0(hour_low_data), .in1(4'b1110), .out(data[19:16]), .sel(and_17_out));
  and and_17 (and_17_out, cli, c_5);
  Multiplexer #(.width(4), .enable("false")) multiplexer_5 (
    .in0(hour_high_data), .in1(4'b1110), .out(data[23:20]), .sel(and_18_out));
  and and_18 (and_18_out, cli, c_6);
  Multiplexer #(.width(4), .enable("false")) multiplexer_6 (
    .in0(sec_high_data), .in1(4'b1110), .out(data[7:4]), .sel(and_14_out));
  and and_19 (res, ~set_mode, ~set_end, b_in[2]);  // AND_Gate
  comparer comparer_1 (.a(data), .b({24{1'b0}}), .same(comparer_1_same));
  D_Flip_Flop d_ff_2 (.D(or_7_out), .clk(clock_3_out), .Q(d_ff_2_q), .reset(alarm));  // open: Qn, preset
  or or_7 (or_7_out, d_ff_2_q, START);
  Clock clock_3 (.out(clock_3_out));
  Clock clock_4 (.out(clock_4_out));
  and and_20 (and_20_out, ~set_mode, b_in[1]);  // AND_Gate
  Clock clock_5 (.out(clock_5_out));
  or or_8 (or_8_out, b_in[2], b_in[0]);
  or or_9 (or_9_out, set_mode, alarm);
  or or_10 (or_10_out, b_in[1], b_in[0], b_in[2]);
  and and_21 (and_21_out, comparer_1_same, d_ff_2_q);
  Clock clock_6 (.out(clock_6_out));
  T_Flip_Flop t_ff_2 (.T(b_in[0]), .clk(clock_4_out), .Q(set_mode), .reset(set_end));  // open: Qn, preset
  T_Flip_Flop t_ff_3 (.T(and_20_out), .clk(clock_5_out), .Q(t_ff_3_q), .reset(or_11_out));  // open: Qn, preset
  or or_11 (or_11_out, or_8_out, or_9_out);
  D_Flip_Flop d_ff_3 (.D(or_12_out), .clk(clock_7_out), .Q(d_ff_3_q), .reset(d_ff_5_q));  // open: Qn, preset
  or or_12 (or_12_out, d_ff_3_q, or_10_out);
  Clock clock_7 (.out(clock_7_out));
  D_Flip_Flop d_ff_4 (.D(and_21_out), .clk(clock_6_out), .Q(alarm));  // open: Qn, preset, reset
  count_512 divider (.EN(t_ff_3_q), .R(or_11_out), .o(START));
  or or_13 (or_13_out, b_in[4], b_in[3]);
  D_Flip_Flop d_ff_5 (.D(or_13_out), .clk(clock_8_out), .Q(d_ff_5_q));  // open: Qn, preset, reset
  Clock clock_8 (.out(clock_8_out));
  and and_22 (nxt, or_13_out, ~d_ff_3_q);  // AND_Gate
  and and_23 (R, d_ff_3_q, or_13_out);

  // Other names for the same wires on the sheet: A_lg = b_in[0]; A_st = b_in[1]; C = b_in[2]; B_lg = b_in[3];
  //   B_st = b_in[4]; dring = alarm
endmodule

module stabilisation (
  input  A,
  input  B,
  output A_L,
  output A_S,
  output C,
  output B_L,
  output B_S
);

  wire A_t, and_1_out, and_2_out, and_3_out, and_4_out, B_t, clock_1_out, clock_2_out, dual, not_1_out,
       not_2_out, t_ff_1_qn;

  not not_1 (not_1_out, A);
  not not_2 (not_2_out, B);
  minimal_dec MIN_A (.Input_1(A), .Output_1(A_t));
  minimal_dec MIN_B (.Input_1(B), .Output_1(B_t));
  and and_1 (and_1_out, A_t, B_t);
  long_dec LONG_A (.EN(A_t), .R(not_1_out), .DUAL(dual), .long(A_L), .short(A_S));
  Clock clock_1 (.out(clock_1_out));
  long_dec LONG_B (.EN(B_t), .R(not_2_out), .DUAL(dual), .long(B_L), .short(B_S));
  and and_2 (and_2_out, and_1_out, t_ff_1_qn);
  T_Flip_Flop t_ff_1 (.T(and_2_out), .clk(clock_1_out), .Q(dual), .Qn(t_ff_1_qn), .reset(C), .preset(1'b0));
  and and_3 (and_3_out, ~A_t, ~B_t);  // AND_Gate
  D_Flip_Flop d_ff_1 (.D(and_4_out), .clk(clock_2_out), .Q(C), .preset(1'b0), .reset(1'b0));  // open: Qn
  and and_4 (and_4_out, dual, and_3_out);
  Clock clock_2 (.out(clock_2_out));

  // Notes on the sheet:
  //   A and B short and long press, C is dual press
endmodule

module long_dec (
  input  EN,
  input  R,
  input  DUAL,
  output long,
  output short
);

  wire and_1_out, and_2_out, and_4_out, and_5_out, and_6_out, and_7_out, and_8_out, and_9_out, and_11_out,
       and_12_out, and_13_out, and_15_out, and_16_out, and_17_out, and_18_out, and_19_out, b_1, b_2, b_3,
       b_4, b_5, carry, clock_1_out, clock_2_out, clock_3_out, clock_4_out, clock_5_out, clock_6_out,
       clock_7_out, d_ff_1_q, d_ff_2_q, d_ff_3_q, d_ff_4_q, d_ff_4_qn, d_ff_5_q, EN_t, INP, j_k_ff_2_q,
       or_1_out, or_2_out, or_3_out, t_ff_1_qn;

  D_Flip_Flop d_ff_1 (.D(R), .clk(clock_1_out), .Q(d_ff_1_q), .preset(1'b0), .reset(1'b0));  // open: Qn
  Clock clock_1 (.out(clock_1_out));
  Clock clock_2 (.out(clock_2_out));
  J_K_Flip_Flop j_k_ff_1 (.J(INP), .K(INP), .clk(clock_2_out), .Q(b_1), .preset(1'b0), .reset(or_1_out));  // open: Qn
  or or_1 (or_1_out, d_ff_1_q, 1'b0);
  Clock clock_3 (.out(clock_3_out));
  count_10 count (.EN(EN), .R(d_ff_1_q), .c_out(INP));  // open: data_o
  T_Flip_Flop t_ff_1 (.T(and_1_out), .clk(clock_3_out), .Qn(t_ff_1_qn), .reset(d_ff_1_q), .preset(1'b0));  // open: Q
  and and_1 (and_1_out, t_ff_1_qn, carry);
  or or_2 (or_2_out, b_1, b_2, b_3, b_4, b_5, carry);
  and and_2 (and_2_out, EN_t, b_1);
  J_K_Flip_Flop j_k_ff_2 (
    .J(and_2_out), .K(and_2_out), .clk(clock_2_out), .Q(j_k_ff_2_q), .preset(1'b0), .reset(or_1_out));  // open: Qn
  and and_3 (EN_t, INP, t_ff_1_qn);
  Clock clock_4 (.out(clock_4_out));
  and and_4 (and_4_out, d_ff_3_q, ~and_8_out);  // AND_Gate
  and and_5 (and_5_out, j_k_ff_2_q, b_1);
  D_Flip_Flop d_ff_2 (.D(DUAL), .clk(clock_5_out), .Q(d_ff_2_q), .preset(1'b0), .reset(1'b0));  // open: Qn
  Clock clock_5 (.out(clock_5_out));
  D_Flip_Flop d_ff_3 (.D(or_3_out), .clk(clock_4_out), .Q(d_ff_3_q), .preset(1'b0), .reset(d_ff_2_q));  // open: Qn
  or or_3 (or_3_out, or_2_out, and_4_out);
  J_K_Flip_Flop j_k_ff_3 (
    .J(and_6_out), .K(and_6_out), .clk(clock_2_out), .Q(b_2), .preset(1'b0), .reset(or_1_out));  // open: Qn
  and and_6 (and_6_out, EN_t, and_5_out);
  and and_7 (and_7_out, and_5_out, b_2);
  and and_8 (and_8_out, d_ff_1_q, ~d_ff_2_q, d_ff_3_q);  // AND_Gate
  J_K_Flip_Flop j_k_ff_4 (
    .J(and_9_out), .K(and_9_out), .clk(clock_2_out), .Q(b_3), .preset(1'b0), .reset(or_1_out));  // open: Qn
  and and_9 (and_9_out, EN_t, and_7_out);
  and and_10 (long, carry, and_8_out);
  and and_11 (and_11_out, ~carry, and_8_out);  // AND_Gate
  and and_12 (and_12_out, d_ff_4_qn, long);
  Clock clock_6 (.out(clock_6_out));
  and and_13 (and_13_out, and_7_out, b_3);
  D_Flip_Flop d_ff_4 (.D(and_12_out), .clk(clock_6_out), .Q(d_ff_4_q), .Qn(d_ff_4_qn), .preset(1'b0), .reset(INP));
  and and_14 (short, ~d_ff_4_q, and_11_out);  // AND_Gate
  J_K_Flip_Flop j_k_ff_5 (
    .J(and_15_out), .K(and_15_out), .clk(clock_2_out), .Q(b_4), .preset(1'b0), .reset(or_1_out));  // open: Qn
  and and_15 (and_15_out, EN_t, and_13_out);
  and and_16 (and_16_out, and_13_out, b_4);
  and and_17 (and_17_out, EN_t, and_16_out);
  J_K_Flip_Flop j_k_ff_6 (
    .J(and_17_out), .K(and_17_out), .clk(clock_2_out), .Q(b_5), .preset(1'b0), .reset(or_1_out));  // open: Qn
  and and_18 (and_18_out, and_16_out, b_5);
  Clock clock_7 (.out(clock_7_out));
  D_Flip_Flop d_ff_5 (.D(or_1_out), .clk(clock_7_out), .Q(d_ff_5_q), .preset(1'b0), .reset(1'b0));  // open: Qn
  J_K_Flip_Flop j_k_ff_7 (
    .J(and_19_out), .K(and_19_out), .clk(clock_2_out), .Q(carry), .preset(1'b0), .reset(d_ff_5_q));  // open: Qn
  and and_19 (and_19_out, EN_t, and_18_out);
endmodule

module minimal_dec (
  input  Input_1,
  output Output_1
);

  wire clock_1_out, d_ff_1_q, d_ff_2_q, d_ff_3_q, d_ff_4_q, d_ff_5_q, d_ff_6_q, d_ff_7_q, not_1_out;

  Clock clock_1 (.out(clock_1_out));
  D_Flip_Flop d_ff_1 (.D(Input_1), .clk(clock_1_out), .Q(d_ff_1_q), .preset(1'b0), .reset(not_1_out));  // open: Qn
  not not_1 (not_1_out, Input_1);
  D_Flip_Flop d_ff_2 (.D(d_ff_1_q), .clk(clock_1_out), .Q(d_ff_2_q), .preset(1'b0), .reset(not_1_out));  // open: Qn
  D_Flip_Flop d_ff_3 (.D(d_ff_2_q), .clk(clock_1_out), .Q(d_ff_3_q), .preset(1'b0), .reset(not_1_out));  // open: Qn
  D_Flip_Flop d_ff_4 (.D(d_ff_3_q), .clk(clock_1_out), .Q(d_ff_4_q), .preset(1'b0), .reset(not_1_out));  // open: Qn
  D_Flip_Flop d_ff_5 (.D(d_ff_4_q), .clk(clock_1_out), .Q(d_ff_5_q), .preset(1'b0), .reset(not_1_out));  // open: Qn
  D_Flip_Flop d_ff_6 (.D(d_ff_5_q), .clk(clock_1_out), .Q(d_ff_6_q), .preset(1'b0), .reset(not_1_out));  // open: Qn
  D_Flip_Flop d_ff_7 (.D(d_ff_6_q), .clk(clock_1_out), .Q(d_ff_7_q), .preset(1'b0), .reset(not_1_out));  // open: Qn
  D_Flip_Flop d_ff_8 (.D(d_ff_7_q), .clk(clock_1_out), .Q(Output_1), .preset(1'b0), .reset(not_1_out));  // open: Qn

  // Notes on the sheet:
  //   Temps minimal avant le déclanchement
endmodule

module count_5 (
  input  EN,
  input  R,
  output o
);

  wire and_1_out, and_3_out, clock_1_out, or_1_out, t_ff_1_q, t_ff_2_q, t_ff_3_q;

  Clock clock_1 (.out(clock_1_out));
  or or_1 (or_1_out, R, and_3_out);
  T_Flip_Flop t_ff_1 (.T(EN), .clk(clock_1_out), .Q(t_ff_1_q), .reset(or_1_out));  // open: Qn, preset
  T_Flip_Flop t_ff_2 (.T(t_ff_1_q), .clk(clock_1_out), .Q(t_ff_2_q), .reset(or_1_out));  // open: Qn, preset
  T_Flip_Flop t_ff_3 (.T(and_1_out), .clk(clock_1_out), .Q(t_ff_3_q), .reset(or_1_out));  // open: Qn, preset
  and and_1 (and_1_out, t_ff_1_q, t_ff_2_q);
  and and_2 (o, ~t_ff_1_q, ~t_ff_2_q, t_ff_3_q);  // AND_Gate
  and and_3 (and_3_out, t_ff_1_q, ~t_ff_2_q, t_ff_3_q);  // AND_Gate
endmodule

module count_6 (
  input  EN,
  input  R,
  output [3:0] data_o,
  output c_out
);

  wire and_1_out, and_2_out, and_3_out, and_4_out, and_5_out, and_6_out, clock_1_out, or_1_out;

  Clock clock_1 (.out(clock_1_out));
  J_K_Flip_Flop j_k_ff_1 (.J(EN), .K(EN), .clk(clock_1_out), .Q(data_o[0]), .reset(or_1_out));  // open: Qn, preset
  or or_1 (or_1_out, R, and_6_out);
  J_K_Flip_Flop j_k_ff_2 (
    .J(and_1_out), .K(and_1_out), .clk(clock_1_out), .Q(data_o[1]), .reset(or_1_out));  // open: Qn, preset
  and and_1 (and_1_out, EN, data_o[0]);
  and and_2 (and_2_out, data_o[1], data_o[0]);
  and and_3 (and_3_out, EN, and_2_out);
  J_K_Flip_Flop j_k_ff_3 (
    .J(and_3_out), .K(and_3_out), .clk(clock_1_out), .Q(data_o[2]), .reset(or_1_out));  // open: Qn, preset
  and and_4 (and_4_out, and_2_out, data_o[2]);
  J_K_Flip_Flop j_k_ff_4 (
    .J(and_5_out), .K(and_5_out), .clk(clock_1_out), .Q(data_o[3]), .reset(or_1_out));  // open: Qn, preset
  and and_5 (and_5_out, EN, and_4_out);
  and and_6 (and_6_out, data_o[2], data_o[1]);
  and and_7 (c_out, data_o[0], EN, data_o[2]);
endmodule

module count_10 (
  input  EN,
  input  R,
  output [3:0] data_o,
  output c_out
);

  wire and_1_out, and_2_out, and_3_out, and_4_out, and_5_out, and_6_out, clock_1_out, or_1_out;

  Clock clock_1 (.out(clock_1_out));
  J_K_Flip_Flop j_k_ff_1 (
    .J(EN), .K(EN), .clk(clock_1_out), .Q(data_o[0]), .preset(1'b0), .reset(or_1_out));  // open: Qn
  or or_1 (or_1_out, R, and_6_out);
  J_K_Flip_Flop j_k_ff_2 (
    .J(and_1_out), .K(and_1_out), .clk(clock_1_out), .Q(data_o[1]), .preset(1'b0), .reset(or_1_out));  // open: Qn
  and and_1 (and_1_out, EN, data_o[0]);
  and and_2 (and_2_out, data_o[1], data_o[0]);
  and and_3 (and_3_out, EN, and_2_out);
  J_K_Flip_Flop j_k_ff_3 (
    .J(and_3_out), .K(and_3_out), .clk(clock_1_out), .Q(data_o[2]), .preset(1'b0), .reset(or_1_out));  // open: Qn
  and and_4 (and_4_out, and_2_out, data_o[2]);
  J_K_Flip_Flop j_k_ff_4 (
    .J(and_5_out), .K(and_5_out), .clk(clock_1_out), .Q(data_o[3]), .preset(1'b0), .reset(or_1_out));  // open: Qn
  and and_5 (and_5_out, EN, and_4_out);
  and and_6 (and_6_out, data_o[1], data_o[3]);
  and and_7 (c_out, data_o[0], EN, data_o[3]);
endmodule

module count_100 (
  input  EN,
  input  R,
  output o
);

  wire and_1_out, and_2_out, and_3_out, and_4_out, and_5_out, and_6_out, and_7_out, and_8_out, and_9_out,
       and_10_out, and_11_out, and_12_out, and_13_out, clock_1_out, j_k_ff_1_q, j_k_ff_2_q, j_k_ff_3_q,
       j_k_ff_4_q, j_k_ff_5_q, j_k_ff_6_q, j_k_ff_7_q, or_1_out;

  Clock clock_1 (.out(clock_1_out));
  J_K_Flip_Flop j_k_ff_1 (.J(EN), .K(EN), .clk(clock_1_out), .Q(j_k_ff_1_q), .reset(or_1_out));  // open: Qn, preset
  and and_1 (and_1_out, j_k_ff_1_q, and_13_out);
  or or_1 (or_1_out, R, and_1_out);
  and and_2 (and_2_out, EN, j_k_ff_1_q);
  J_K_Flip_Flop j_k_ff_2 (
    .J(and_2_out), .K(and_2_out), .clk(clock_1_out), .Q(j_k_ff_2_q), .reset(or_1_out));  // open: Qn, preset
  and and_3 (and_3_out, j_k_ff_2_q, j_k_ff_1_q);
  and and_4 (and_4_out, EN, and_3_out);
  J_K_Flip_Flop j_k_ff_3 (
    .J(and_4_out), .K(and_4_out), .clk(clock_1_out), .Q(j_k_ff_3_q), .reset(or_1_out));  // open: Qn, preset
  and and_5 (and_5_out, and_3_out, j_k_ff_3_q);
  J_K_Flip_Flop j_k_ff_4 (
    .J(and_6_out), .K(and_6_out), .clk(clock_1_out), .Q(j_k_ff_4_q), .reset(or_1_out));  // open: Qn, preset
  and and_6 (and_6_out, EN, and_5_out);
  and and_7 (and_7_out, and_5_out, j_k_ff_4_q);
  J_K_Flip_Flop j_k_ff_5 (
    .J(and_8_out), .K(and_8_out), .clk(clock_1_out), .Q(j_k_ff_5_q), .reset(or_1_out));  // open: Qn, preset
  and and_8 (and_8_out, EN, and_7_out);
  and and_9 (and_9_out, and_7_out, j_k_ff_5_q);
  and and_10 (and_10_out, EN, and_9_out);
  J_K_Flip_Flop j_k_ff_6 (
    .J(and_10_out), .K(and_10_out), .clk(clock_1_out), .Q(j_k_ff_6_q), .reset(or_1_out));  // open: Qn, preset
  and and_11 (and_11_out, and_9_out, j_k_ff_6_q);
  J_K_Flip_Flop j_k_ff_7 (
    .J(and_12_out), .K(and_12_out), .clk(clock_1_out), .Q(j_k_ff_7_q), .reset(or_1_out));  // open: Qn, preset
  and and_12 (and_12_out, EN, and_11_out);
  and and_13 (and_13_out, ~j_k_ff_1_q, ~j_k_ff_2_q, j_k_ff_3_q, ~j_k_ff_4_q, ~j_k_ff_5_q, j_k_ff_6_q, j_k_ff_7_q);  // AND_Gate
  and and_14 (o, j_k_ff_1_q, j_k_ff_2_q, ~j_k_ff_3_q, ~j_k_ff_4_q, ~j_k_ff_5_q, j_k_ff_6_q, j_k_ff_7_q);  // AND_Gate

  // Notes on the sheet:
  //   count to 100 - used for 1024Hz input
endmodule

module count_128 (
  input  EN,
  input  R,
  output c_out
);

  wire and_1_out, and_2_out, and_3_out, and_4_out, and_5_out, and_6_out, and_7_out, and_8_out, and_9_out,
       and_10_out, and_11_out, and_12_out, clock_1_out, j_k_ff_1_q, j_k_ff_2_q, j_k_ff_3_q, j_k_ff_4_q,
       j_k_ff_5_q, j_k_ff_6_q, or_1_out;

  Clock clock_1 (.out(clock_1_out));
  J_K_Flip_Flop j_k_ff_1 (.J(EN), .K(EN), .clk(clock_1_out), .Q(j_k_ff_1_q), .reset(or_1_out));  // open: Qn, preset
  or or_1 (or_1_out, R, and_1_out);
  and and_1 (and_1_out, j_k_ff_1_q, c_out);
  and and_2 (and_2_out, EN, j_k_ff_1_q);
  J_K_Flip_Flop j_k_ff_2 (
    .J(and_2_out), .K(and_2_out), .clk(clock_1_out), .Q(j_k_ff_2_q), .reset(or_1_out));  // open: Qn, preset
  and and_3 (and_3_out, j_k_ff_2_q, j_k_ff_1_q);
  J_K_Flip_Flop j_k_ff_3 (
    .J(and_4_out), .K(and_4_out), .clk(clock_1_out), .Q(j_k_ff_3_q), .reset(or_1_out));  // open: Qn, preset
  and and_4 (and_4_out, EN, and_3_out);
  and and_5 (and_5_out, and_3_out, j_k_ff_3_q);
  J_K_Flip_Flop j_k_ff_4 (
    .J(and_6_out), .K(and_6_out), .clk(clock_1_out), .Q(j_k_ff_4_q), .reset(or_1_out));  // open: Qn, preset
  and and_6 (and_6_out, EN, and_5_out);
  and and_7 (and_7_out, and_5_out, j_k_ff_4_q);
  J_K_Flip_Flop j_k_ff_5 (
    .J(and_8_out), .K(and_8_out), .clk(clock_1_out), .Q(j_k_ff_5_q), .reset(or_1_out));  // open: Qn, preset
  and and_8 (and_8_out, EN, and_7_out);
  and and_9 (and_9_out, and_7_out, j_k_ff_5_q);
  and and_10 (and_10_out, EN, and_9_out);
  J_K_Flip_Flop j_k_ff_6 (
    .J(and_10_out), .K(and_10_out), .clk(clock_1_out), .Q(j_k_ff_6_q), .reset(or_1_out));  // open: Qn, preset
  and and_11 (and_11_out, and_9_out, j_k_ff_6_q);
  J_K_Flip_Flop j_k_ff_7 (
    .J(and_12_out), .K(and_12_out), .clk(clock_1_out), .Q(c_out), .reset(or_1_out));  // open: Qn, preset
  and and_12 (and_12_out, EN, and_11_out);
endmodule

module count_512 (
  input  EN,
  input  R,
  output o
);

  wire and_1_out, and_2_out, and_3_out, and_4_out, and_5_out, and_6_out, and_7_out, and_8_out, and_9_out,
       and_10_out, and_11_out, and_12_out, and_13_out, and_14_out, and_15_out, clock_1_out, t_ff_1_q,
       t_ff_2_q, t_ff_3_q, t_ff_4_q, t_ff_5_q, t_ff_6_q, t_ff_7_q, t_ff_8_q, t_ff_9_q;

  Clock clock_1 (.out(clock_1_out));
  and and_1 (and_1_out, t_ff_1_q, EN);
  and and_2 (and_2_out, and_9_out, EN);
  and and_3 (and_3_out, and_10_out, EN);
  and and_4 (and_4_out, and_11_out, EN);
  and and_5 (and_5_out, and_12_out, EN);
  and and_6 (and_6_out, and_13_out, EN);
  and and_7 (and_7_out, and_14_out, EN);
  and and_8 (and_8_out, and_15_out, EN);
  T_Flip_Flop t_ff_1 (.T(EN), .clk(clock_1_out), .Q(t_ff_1_q), .reset(R), .preset(1'b0));  // open: Qn
  T_Flip_Flop t_ff_2 (.T(and_1_out), .clk(clock_1_out), .Q(t_ff_2_q), .reset(R), .preset(1'b0));  // open: Qn
  T_Flip_Flop t_ff_3 (.T(and_2_out), .clk(clock_1_out), .Q(t_ff_3_q), .reset(R), .preset(1'b0));  // open: Qn
  T_Flip_Flop t_ff_4 (.T(and_3_out), .clk(clock_1_out), .Q(t_ff_4_q), .reset(R), .preset(1'b0));  // open: Qn
  T_Flip_Flop t_ff_5 (.T(and_4_out), .clk(clock_1_out), .Q(t_ff_5_q), .reset(R), .preset(1'b0));  // open: Qn
  T_Flip_Flop t_ff_6 (.T(and_5_out), .clk(clock_1_out), .Q(t_ff_6_q), .reset(R), .preset(1'b0));  // open: Qn
  T_Flip_Flop t_ff_7 (.T(and_6_out), .clk(clock_1_out), .Q(t_ff_7_q), .reset(R), .preset(1'b0));  // open: Qn
  T_Flip_Flop t_ff_8 (.T(and_7_out), .clk(clock_1_out), .Q(t_ff_8_q), .reset(R), .preset(1'b0));  // open: Qn
  T_Flip_Flop t_ff_9 (.T(and_8_out), .clk(clock_1_out), .Q(t_ff_9_q), .reset(R), .preset(1'b0));  // open: Qn
  and and_9 (and_9_out, t_ff_2_q, t_ff_1_q);
  and and_10 (and_10_out, t_ff_3_q, and_9_out);
  and and_11 (and_11_out, t_ff_4_q, and_10_out);
  and and_12 (and_12_out, t_ff_5_q, and_11_out);
  and and_13 (and_13_out, t_ff_6_q, and_12_out);
  and and_14 (and_14_out, t_ff_7_q, and_13_out);
  and and_15 (and_15_out, t_ff_8_q, and_14_out);
  and and_16 (o, t_ff_9_q, and_15_out, and_14_out, and_13_out, and_12_out, and_11_out, and_10_out, and_9_out, t_ff_1_q);

  // Notes on the sheet:
  //   count to 100 - used for 1024Hz input
endmodule

module seven (
  input  [3:0] Input_bus_1,
  input  [3:0] d_day,
  input  day,
  input  [1:0] monthType,
  output cen,
  output l_h,
  output top,
  output r_h,
  output l_b,
  output bot,
  output r_b
);

  wire a1, a2, a3, and_1_out, and_2_out, and_3_out, and_4_out, and_5_out, and_6_out, and_7_out, and_8_out,
       and_9_out, and_10_out, and_11_out, and_12_out, and_13_out, and_14_out, and_15_out, and_16_out,
       and_17_out, and_18_out, and_19_out, and_20_out, and_21_out, and_22_out, and_23_out, and_24_out, b1,
       b2, b3, c1, c2, c3, d1, d2, d3, e1, e2, e3, f1, f2, f3, g1, g2, g3, not_1_out, not_2_out, not_3_out,
       not_4_out, not_5_out, not_6_out, not_7_out, not_8_out, not_9_out, not_10_out, not_11_out, not_12_out,
       not_13_out, not_14_out, not_15_out, not_16_out, not_17_out, not_18_out, not_19_out, not_20_out,
       not_21_out, not_22_out, not_23_out, not_24_out, not_25_out, not_26_out, not_27_out, not_28_out,
       not_29_out, not_30_out, not_31_out, not_32_out, not_33_out, not_34_out, not_35_out, or_1_out,
       or_2_out, or_3_out, or_4_out, or_5_out, or_6_out, or_7_out;
  wire [1:0] typ;
  wire [3:0] demultiplexer_1_out0, month_d_hi, month_d_low, month_d_mid, multiplexer_1_out;

  Multiplexer #(.width(4), .enable("false")) multiplexer_1 (
    .in0(Input_bus_1), .in1(d_day), .out(multiplexer_1_out), .sel(day));
  not not_1 (not_1_out, day);
  Multiplexer #(.width(2), .enable("false")) multiplexer_2 (.in0(monthType), .in1(2'b00), .out(typ), .sel(not_1_out));
  Demultiplexer #(.select(2), .width(4), .enable("false")) demultiplexer_1 (
    .out0(demultiplexer_1_out0), .out1(month_d_low), .out2(month_d_mid), .out3(month_d_hi),
    .in(multiplexer_1_out), .sel(typ));
  fst_letter low_let (
    .month_num(month_d_low), .cnt(a1), .left_h(b1), .top(c1), .right_h(d1), .left_bt(e1), .bt(f1),
    .right_bt(g1));
  mid_letter mid_let (
    .month_num(month_d_mid), .cnt(a2), .lft_high(b2), .top(c2), .right_h(d2), .left_bt(e2), .bt(f2),
    .right_bt(g2));
  thd_letter high_let (
    .month_num(month_d_hi), .cnt(a3), .left_h(b3), .top(c3), .right_h(d3), .left_bottom(e3), .bt(f3),
    .right_bt(g3));
  not not_2 (not_2_out, demultiplexer_1_out0[2]);
  and and_1 (and_1_out, not_2_out, demultiplexer_1_out0[1]);
  not not_3 (not_3_out, demultiplexer_1_out0[3]);
  and and_2 (and_2_out, not_3_out, demultiplexer_1_out0[2], not_4_out);
  not not_4 (not_4_out, demultiplexer_1_out0[0]);
  and and_3 (and_3_out, demultiplexer_1_out0[2], not_5_out);
  not not_5 (not_5_out, demultiplexer_1_out0[1]);
  and and_4 (and_4_out, demultiplexer_1_out0[3], not_6_out);
  not not_6 (not_6_out, demultiplexer_1_out0[2]);
  and and_5 (and_5_out, demultiplexer_1_out0[3], demultiplexer_1_out0[0]);
  not not_7 (not_7_out, demultiplexer_1_out0[1]);
  and and_6 (and_6_out, not_7_out, not_8_out);
  not not_8 (not_8_out, demultiplexer_1_out0[0]);
  not not_9 (not_9_out, demultiplexer_1_out0[3]);
  and and_7 (and_7_out, not_9_out, demultiplexer_1_out0[2], not_10_out);
  not not_10 (not_10_out, demultiplexer_1_out0[0]);
  and and_8 (and_8_out, demultiplexer_1_out0[2], not_11_out);
  not not_11 (not_11_out, demultiplexer_1_out0[1]);
  and and_9 (and_9_out, demultiplexer_1_out0[3], not_12_out);
  not not_12 (not_12_out, demultiplexer_1_out0[2]);
  not not_13 (not_13_out, demultiplexer_1_out0[2]);
  and and_10 (and_10_out, not_13_out, not_14_out);
  not not_14 (not_14_out, demultiplexer_1_out0[0]);
  not not_15 (not_15_out, demultiplexer_1_out0[3]);
  and and_11 (and_11_out, not_15_out, demultiplexer_1_out0[1]);
  not not_16 (not_16_out, demultiplexer_1_out0[3]);
  and and_12 (and_12_out, not_16_out, demultiplexer_1_out0[2], demultiplexer_1_out0[0]);
  and and_13 (and_13_out, demultiplexer_1_out0[3], not_17_out);
  not not_17 (not_17_out, demultiplexer_1_out0[2]);
  not not_18 (not_18_out, demultiplexer_1_out0[2]);
  not not_19 (not_19_out, demultiplexer_1_out0[1]);
  and and_14 (and_14_out, not_19_out, not_20_out);
  not not_20 (not_20_out, demultiplexer_1_out0[0]);
  not not_21 (not_21_out, demultiplexer_1_out0[3]);
  and and_15 (and_15_out, not_21_out, demultiplexer_1_out0[1], demultiplexer_1_out0[0]);
  not not_22 (not_22_out, demultiplexer_1_out0[2]);
  and and_16 (and_16_out, not_22_out, not_23_out);
  not not_23 (not_23_out, demultiplexer_1_out0[0]);
  not not_24 (not_24_out, demultiplexer_1_out0[3]);
  and and_17 (and_17_out, not_24_out, demultiplexer_1_out0[1], not_25_out);
  not not_25 (not_25_out, demultiplexer_1_out0[0]);
  not not_26 (not_26_out, demultiplexer_1_out0[2]);
  and and_18 (and_18_out, not_26_out, not_27_out);
  not not_27 (not_27_out, demultiplexer_1_out0[0]);
  not not_28 (not_28_out, demultiplexer_1_out0[3]);
  and and_19 (and_19_out, not_28_out, demultiplexer_1_out0[1], not_29_out);
  not not_29 (not_29_out, demultiplexer_1_out0[0]);
  not not_30 (not_30_out, demultiplexer_1_out0[2]);
  and and_20 (and_20_out, not_30_out, demultiplexer_1_out0[1]);
  not not_31 (not_31_out, demultiplexer_1_out0[1]);
  and and_21 (and_21_out, demultiplexer_1_out0[2], not_31_out, demultiplexer_1_out0[0]);
  and and_22 (and_22_out, demultiplexer_1_out0[3], not_32_out);
  not not_32 (not_32_out, demultiplexer_1_out0[2]);
  not not_33 (not_33_out, demultiplexer_1_out0[1]);
  not not_34 (not_34_out, demultiplexer_1_out0[3]);
  and and_23 (and_23_out, not_34_out, demultiplexer_1_out0[0]);
  not not_35 (not_35_out, demultiplexer_1_out0[3]);
  and and_24 (and_24_out, not_35_out, demultiplexer_1_out0[2]);
  or or_1 (or_1_out, and_1_out, and_2_out, and_3_out, and_4_out, and_5_out);
  or or_2 (or_2_out, and_6_out, and_7_out, and_8_out, and_9_out);
  or or_3 (or_3_out, and_10_out, and_11_out, and_12_out, and_13_out);
  or or_4 (or_4_out, not_18_out, and_14_out, and_15_out);
  or or_5 (or_5_out, and_16_out, and_17_out);
  or or_6 (or_6_out, and_18_out, and_19_out, and_20_out, and_21_out, and_22_out);
  or or_7 (or_7_out, not_33_out, and_23_out, and_24_out);
  Multiplexer #(.select(2), .enable("false")) multiplexer_3 (
    .in0(or_1_out), .in1(a1), .in2(a2), .in3(a3), .out(cen), .sel(typ));
  Multiplexer #(.select(2), .enable("false")) multiplexer_4 (
    .in0(or_2_out), .in1(b1), .in2(b2), .in3(b3), .out(l_h), .sel(typ));
  Multiplexer #(.select(2), .enable("false")) multiplexer_5 (
    .in0(or_3_out), .in1(c1), .in2(c2), .in3(c3), .out(top), .sel(typ));
  Multiplexer #(.select(2), .enable("false")) multiplexer_6 (
    .in0(or_4_out), .in1(d1), .in2(d2), .in3(d3), .out(r_h), .sel(typ));
  Multiplexer #(.select(2), .enable("false")) multiplexer_7 (
    .in0(or_5_out), .in1(e1), .in2(e2), .in3(e3), .out(l_b), .sel(typ));
  Multiplexer #(.select(2), .enable("false")) multiplexer_8 (
    .in0(or_6_out), .in1(f1), .in2(f2), .in3(f3), .out(bot), .sel(typ));
  Multiplexer #(.select(2), .enable("false")) multiplexer_9 (
    .in0(or_7_out), .in1(g1), .in2(g2), .in3(g3), .out(r_b), .sel(typ));
endmodule

module button_array (
  input  A_L,
  input  A_S,
  input  C,
  input  B_L,
  input  B_S,
  output [4:0] o
);


  assign o = {B_S, B_L, C, A_S, A_L};
endmodule

module mode_conv (
  input  [1:0] i,
  output zero,
  output one,
  output two,
  output three
);

  and three_b01969a8 (three, i[0], i[1]);
  and one_518f7fc6 (one, i[0], ~i[1]);  // AND_Gate
  and two_f7353909 (two, i[1], ~i[0]);  // AND_Gate
  and zero_5fd7b8a2 (zero, ~i[0], ~i[1]);  // AND_Gate
endmodule

module bidirectionnal_10 (
  input  EN,
  input  UP,
  input  R,
  output [3:0] data,
  output carry
);

  wire and_1_out, and_2_out, and_3_out, and_4_out, and_5_out, and_6_out, and_7_out, and_8_out, and_9_out,
       and_11_out, and_13_out, clock_1_out, or_1_out, or_2_out, or_3_out, or_4_out, or_5_out, or_6_out,
       or_7_out, res, set_10, t_ff_1_qn, t_ff_2_qn, t_ff_3_qn;

  Clock clock_1 (.out(clock_1_out));
  T_Flip_Flop t_ff_1 (.T(EN), .clk(clock_1_out), .Q(data[0]), .Qn(t_ff_1_qn), .reset(or_1_out), .preset(set_10));
  or or_1 (or_1_out, R, res);
  and and_1 (and_1_out, UP, data[0]);
  or or_2 (or_2_out, and_1_out, and_2_out);
  and and_2 (and_2_out, t_ff_1_qn, ~UP);  // AND_Gate
  and and_3 (and_3_out, EN, or_2_out);
  T_Flip_Flop t_ff_2 (.T(and_3_out), .clk(clock_1_out), .Q(data[1]), .Qn(t_ff_2_qn), .reset(or_3_out), .preset(1'b0));
  or or_3 (or_3_out, set_10, or_1_out);
  and and_4 (and_4_out, and_1_out, data[1]);
  or or_4 (or_4_out, and_4_out, and_5_out);
  and and_5 (and_5_out, t_ff_2_qn, and_2_out);
  and and_6 (and_6_out, EN, or_4_out);
  T_Flip_Flop t_ff_3 (.T(and_6_out), .clk(clock_1_out), .Q(data[2]), .Qn(t_ff_3_qn), .reset(or_5_out), .preset(1'b0));
  or or_5 (or_5_out, set_10, or_1_out);
  and and_7 (and_7_out, data[2], and_4_out);
  and and_8 (and_8_out, and_5_out, t_ff_3_qn);
  and and_9 (and_9_out, EN, or_6_out);
  or or_6 (or_6_out, and_7_out, and_8_out);
  T_Flip_Flop t_ff_4 (.T(and_9_out), .clk(clock_1_out), .Q(data[3]), .reset(or_1_out), .preset(set_10));  // open: Qn
  and and_10 (set_10, ~UP, data[0], data[1], data[2], data[3]);  // AND_Gate
  and and_11 (and_11_out, ~data[0], ~data[1], ~data[2], ~data[3], ~UP);  // AND_Gate
  and and_12 (res, UP, ~data[0], data[1], ~data[2], data[3]);  // AND_Gate
  and and_13 (and_13_out, data[3], ~data[2], ~data[1], data[0], UP);  // AND_Gate
  or or_7 (or_7_out, and_13_out, and_11_out);
  and and_14 (carry, EN, or_7_out);
endmodule

module bidirectionnal_6 (
  input  EN,
  input  UP,
  input  R,
  output [3:0] data,
  output carry
);

  wire and_1_out, and_2_out, and_3_out, and_4_out, and_5_out, and_6_out, and_7_out, and_8_out, and_9_out,
       and_11_out, and_13_out, clock_1_out, or_1_out, or_2_out, or_3_out, or_4_out, or_5_out, or_6_out,
       or_7_out, res, set_6, t_ff_1_qn, t_ff_2_qn, t_ff_3_qn;

  Clock clock_1 (.out(clock_1_out));
  T_Flip_Flop t_ff_1 (.T(EN), .clk(clock_1_out), .Q(data[0]), .Qn(t_ff_1_qn), .reset(or_1_out), .preset(set_6));
  or or_1 (or_1_out, R, res);
  and and_1 (and_1_out, UP, data[0]);
  or or_2 (or_2_out, and_1_out, and_2_out);
  and and_2 (and_2_out, t_ff_1_qn, ~UP);  // AND_Gate
  T_Flip_Flop t_ff_2 (.T(and_3_out), .clk(clock_1_out), .Q(data[1]), .Qn(t_ff_2_qn), .reset(or_3_out), .preset(1'b0));
  and and_3 (and_3_out, EN, or_2_out);
  or or_3 (or_3_out, set_6, or_1_out);
  and and_4 (and_4_out, and_1_out, data[1]);
  or or_4 (or_4_out, and_4_out, and_5_out);
  and and_5 (and_5_out, t_ff_2_qn, and_2_out);
  and and_6 (and_6_out, EN, or_4_out);
  T_Flip_Flop t_ff_3 (.T(and_6_out), .clk(clock_1_out), .Q(data[2]), .Qn(t_ff_3_qn), .reset(or_1_out), .preset(set_6));
  and and_7 (and_7_out, data[2], and_4_out);
  and and_8 (and_8_out, and_5_out, t_ff_3_qn);
  and and_9 (and_9_out, EN, or_5_out);
  or or_5 (or_5_out, and_7_out, and_8_out);
  T_Flip_Flop t_ff_4 (.T(and_9_out), .clk(clock_1_out), .Q(data[3]), .reset(or_6_out), .preset(1'b0));  // open: Qn
  or or_6 (or_6_out, set_6, or_1_out);
  and and_10 (set_6, ~UP, data[0], data[1], data[2], data[3]);  // AND_Gate
  and and_11 (and_11_out, ~data[0], ~data[1], ~data[2], ~data[3], ~UP);  // AND_Gate
  and and_12 (res, UP, ~data[0], data[1], data[2], ~data[3]);  // AND_Gate
  and and_13 (and_13_out, ~data[3], data[2], ~data[1], data[0], UP);  // AND_Gate
  or or_7 (or_7_out, and_13_out, and_11_out);
  and and_14 (carry, EN, or_7_out);
endmodule

module comparer (
  input  [23:0] a,
  input  [23:0] b,
  output same
);

  wire comparer_4_1_same, comparer_4_2_same, comparer_4_3_same, comparer_4_4_same, comparer_4_5_same,
       comparer_4_6_same;

  comparer_4 comparer_4_1 (.a(a[3:0]), .b(b[3:0]), .same(comparer_4_1_same));
  comparer_4 comparer_4_2 (.a(a[7:4]), .b(b[7:4]), .same(comparer_4_2_same));
  comparer_4 comparer_4_3 (.a(a[11:8]), .b(b[11:8]), .same(comparer_4_3_same));
  comparer_4 comparer_4_4 (.a(a[15:12]), .b(b[15:12]), .same(comparer_4_4_same));
  comparer_4 comparer_4_5 (.a(a[19:16]), .b(b[19:16]), .same(comparer_4_5_same));
  comparer_4 comparer_4_6 (.a(a[23:20]), .b(b[23:20]), .same(comparer_4_6_same));
  and and_1 (same, comparer_4_1_same, comparer_4_2_same, comparer_4_3_same, comparer_4_4_same, comparer_4_5_same, comparer_4_6_same);
endmodule

module comparer_4 (
  input  [3:0] a,
  input  [3:0] b,
  output same
);

  wire or_1_out, or_2_out, xor_1_out, xor_2_out, xor_3_out, xor_4_out;

  xor xor_1 (xor_1_out, a[0], b[0]);
  xor xor_2 (xor_2_out, a[1], b[1]);
  xor xor_3 (xor_3_out, a[2], b[2]);
  xor xor_4 (xor_4_out, a[3], b[3]);
  or or_1 (or_1_out, xor_1_out, xor_2_out);
  or or_2 (or_2_out, xor_3_out, xor_4_out);
  nor nor_1 (same, or_1_out, or_2_out);
endmodule
