// Logisim project time.circ as structural Verilog: 16 circuits, main circuit clocker
module clocker (
  input  set_mode,
  input  but_in,
  input  next_digit,
  input  time_or_date,
  input  R,
  output [3:0] high_hour,
  output [3:0] low_hour,
  output [3:0] high_min,
  output [3:0] low_min,
  output [3:0] high_sec,
  output [3:0] low_sec,
  output [3:0] low_day,
  output [3:0] high_day,
  output [3:0] month_val
);

  wire activate_date, activate_time, clock_1_out, time_keeping_1_nv_jour;

  Clock clock_1 (.out(clock_1_out));
  Demultiplexer #(.enable("false")) demultiplexer_1 (
    .out0(activate_time), .out1(activate_date), .in(1'b1), .sel(time_or_date));
  time_keeping time_keeping_1 (
    .set_mode(set_mode), .but_in(but_in), .CLK_input(clock_1_out), .next_digit(next_digit), .R(R),
    .high_hour(high_hour), .low_hour(low_hour), .high_minute(high_min), .low_minute(low_min),
    .high_second(high_sec), .low_second(low_sec), .nv_jour(time_keeping_1_nv_jour));
  date date_1 (
    .enable(time_keeping_1_nv_jour), .CLK_input(clock_1_out), .Low_day(low_day), .High_day(high_day),
    .month_numerical_value(month_val));
endmodule

module time_keeping (
  input  set_mode,
  input  but_in,
  input  CLK_input,
  input  next_digit,
  input  R,
  output [3:0] high_hour,
  output [3:0] low_hour,
  output [3:0] high_minute,
  output [3:0] low_minute,
  output [3:0] high_second,
  output [3:0] low_second,
  output nv_jour
);

  wire and_1_out, and_2_out, and_3_out, and_4_out, and_5_out, and_6_out, and_7_out, clock_1_out,
       count_100_t_1_output_1, demultiplexer_1_out0, demultiplexer_1_out1, demultiplexer_1_out2,
       demultiplexer_1_out3, demultiplexer_1_out4, demultiplexer_1_out6, demultiplexer_1_out7,
       minutes_counter_1_c_out, mycount_1_c, not_1_out, not_2_out, or_1_out, or_2_out,
       seconds_counter_1_s_c_out, t_ff_1_q, t_ff_2_qn;
  wire [2:0] add_4_bits_1_out_put;
  wire [3:0] hours_counter_1_st_hr, hours_counter_1_wk_hr, minutes_counter_1_m1_out,
       minutes_counter_1_m2_out, seconds_counter_1_s1_output, seconds_counter_1_s2_output;
  wire [3:3] add_4_bits_1_out_put_2;

  T_Flip_Flop t_ff_1 (.T(set_mode), .clk(CLK_input), .Q(t_ff_1_q), .reset(R));  // open: Qn, preset
  Demultiplexer #(.select(3), .enable("false")) demultiplexer_1 (
    .out0(demultiplexer_1_out0), .out1(demultiplexer_1_out1), .out2(demultiplexer_1_out2),
    .out3(demultiplexer_1_out3), .out4(demultiplexer_1_out4), .out6(demultiplexer_1_out6),
    .out7(demultiplexer_1_out7), .in(t_ff_1_q), .sel(add_4_bits_1_out_put));  // open: out5
  and and_1 (and_1_out, t_ff_1_q, but_in, demultiplexer_1_out0);
  add_4_bits add_4_bits_1 (
    .enable(next_digit), .CLK_input(CLK_input), .Reset(demultiplexer_1_out6),
    .out_put({add_4_bits_1_out_put_2[3], add_4_bits_1_out_put}));
  not not_1 (not_1_out, t_ff_1_q);
  or or_1 (or_1_out, not_1_out, and_1_out);
  and and_2 (and_2_out, t_ff_1_q, but_in, demultiplexer_1_out1);
  and and_3 (and_3_out, t_ff_1_q, but_in, demultiplexer_1_out2);
  and and_4 (and_4_out, t_ff_1_q, but_in, demultiplexer_1_out3);
  and and_5 (and_5_out, t_ff_1_q, but_in, demultiplexer_1_out4);
  and and_6 (and_6_out, t_ff_1_q, but_in, demultiplexer_1_out7);
  and and_7 (and_7_out, t_ff_1_q, or_1_out);
  count_512_t mycount_1 (.EN(or_1_out), .R(1'b0), .c(mycount_1_c));
  or or_2 (or_2_out, and_7_out, mycount_1_c);
  seconds_counter seconds_counter_1 (
    .run_wk_s(or_2_out), .CLK_input(CLK_input), .run_st_s(and_2_out), .set_mode(t_ff_1_q),
    .s1_output(seconds_counter_1_s1_output), .s_c_out(seconds_counter_1_s_c_out),
    .s2_output(seconds_counter_1_s2_output));
  minutes_counter minutes_counter_1 (
    .run_wk_mn(and_3_out), .c_in(seconds_counter_1_s_c_out), .CLK_input(CLK_input), .run_st_mn(and_4_out),
    .m1_out(minutes_counter_1_m1_out), .m2_out(minutes_counter_1_m2_out), .c_out(minutes_counter_1_c_out));
  hours_counter hours_counter_1 (
    .run_st_hr(and_6_out), .run_wk_hr(and_5_out), .CLK_input(CLK_input), .c_in_m(minutes_counter_1_c_out),
    .c_in_s(seconds_counter_1_s_c_out), .set_mode(t_ff_1_q), .c_out(nv_jour), .st_hr(hours_counter_1_st_hr),
    .wk_hr(hours_counter_1_wk_hr));
  T_Flip_Flop t_ff_2 (
    .T(count_100_t_1_output_1), .clk(clock_1_out), .Qn(t_ff_2_qn), .reset(not_2_out));  // open: Q, preset
  count_100_t count_100_t_1 (.EN(t_ff_1_q), .R(not_2_out), .Output_1(count_100_t_1_output_1));
  Clock clock_1 (.out(clock_1_out));
  not not_2 (not_2_out, t_ff_1_q);
  Multiplexer #(.width(4), .enable("false")) multiplexer_1 (
    .in0(4'b1110), .in1(hours_counter_1_st_hr), .out(high_hour), .sel(t_ff_2_qn));
  Multiplexer #(.width(4), .enable("false")) multiplexer_2 (
    .in0(4'b1110), .in1(hours_counter_1_wk_hr), .out(low_hour), .sel(t_ff_2_qn));
  Multiplexer #(.width(4), .enable("false")) multiplexer_3 (
    .in0(4'b1110), .in1(minutes_counter_1_m2_out), .out(high_minute), .sel(t_ff_2_qn));
  Multiplexer #(.width(4), .enable("false")) multiplexer_4 (
    .in0(4'b1110), .in1(minutes_counter_1_m1_out), .out(low_minute), .sel(t_ff_2_qn));
  Multiplexer #(.width(4), .enable("false")) multiplexer_5 (
    .in0(4'b1110), .in1(seconds_counter_1_s1_output), .out(low_second), .sel(t_ff_2_qn));
  Multiplexer #(.width(4), .enable("false")) multiplexer_6 (
    .in0(4'b1110), .in1(seconds_counter_1_s2_output), .out(high_second), .sel(t_ff_2_qn));

  // Other names for the same wires on the sheet: res = R
endmodule

module seconds_counter (
  input  run_wk_s,
  input  CLK_input,
  input  run_st_s,
  input  set_mode,
  output [3:0] s1_output,
  output s_c_out,
  output [3:0] s2_output
);

  wire and_1_out, and_4_out, and_5_out, and_6_out, and_7_out, not_1_out, or_1_out, out_1, out_2;

  not not_1 (not_1_out, set_mode);
  and and_1 (and_1_out, out_1, not_1_out);
  and and_2 (out_1, and_4_out, run_wk_s);
  and and_3 (s_c_out, and_6_out, run_wk_s);
  or or_1 (or_1_out, run_st_s, and_1_out);
  and and_4 (and_4_out, s1_output[0], s1_output[3]);
  and and_5 (and_5_out, s1_output[1], s1_output[3]);
  add_4_bits add_4_bits_1 (.enable(run_wk_s), .CLK_input(CLK_input), .Reset(and_5_out), .out_put(s1_output));
  and and_6 (and_6_out, and_4_out, and_7_out);
  add_4_bits add_4_bits_2 (.enable(or_1_out), .CLK_input(CLK_input), .Reset(out_2), .out_put(s2_output));
  and and_7 (and_7_out, s2_output[0], s2_output[2]);
  and and_8 (out_2, s2_output[1], s2_output[2]);

  // Other names for the same wires on the sheet: c_out = s_c_out; EN = run_wk_s
endmodule

module minutes_counter (
  input  run_wk_mn,
  input  c_in,
  input  CLK_input,
  input  run_st_mn,
  output [3:0] m1_out,
  output [3:0] m2_out,
  output c_out
);

  wire and_1_out, and_4_out, and_5_out, and_6_out, EN, or_2_out, out_4, out_5;

  and and_1 (and_1_out, c_in, out_4);
  or or_1 (EN, run_wk_mn, c_in);
  or or_2 (or_2_out, run_st_mn, and_1_out);
  and and_2 (out_4, EN, and_4_out);
  and and_3 (c_out, out_4, and_6_out);
  and and_4 (and_4_out, m1_out[3], m1_out[0]);
  and and_5 (and_5_out, m1_out[3], m1_out[1]);
  add_4_bits add_4_bits_1 (.enable(EN), .CLK_input(CLK_input), .Reset(and_5_out), .out_put(m1_out));
  and and_6 (and_6_out, m2_out[0], EN, m2_out[2]);
  add_4_bits add_4_bits_2 (.enable(or_2_out), .CLK_input(CLK_input), .Reset(out_5), .out_put(m2_out));
  and and_7 (out_5, m2_out[2], m2_out[1]);

  // Notes on the sheet:
  //   is c_in alright ?
endmodule

module hours_counter (
  input  run_st_hr,
  input  run_wk_hr,
  input  CLK_input,
  input  c_in_m,
  input  c_in_s,
  input  set_mode,
  output c_out,
  output [3:0] st_hr,
  output [3:0] wk_hr
);

  wire and_1_out, and_2_out, and_4_out, and_5_out, and_6_out, and_9_out, incr_1, incr_2, not_1_out, or_1_out,
       or_2_out, or_3_out, or_4_out, out_6, out_7, reset, reset_impulse;

  not not_1 (not_1_out, set_mode);
  and and_1 (and_1_out, and_2_out, incr_2);
  and and_2 (and_2_out, c_in_m, c_in_s, not_1_out);
  or or_1 (or_1_out, reset, reset_impulse, out_7);
  or or_2 (or_2_out, run_st_hr, and_1_out);
  or or_3 (or_3_out, reset, reset_impulse, out_6);
  or or_4 (or_4_out, run_wk_hr, and_2_out);
  add_4_bits add_4_bits_1 (.enable(or_2_out), .CLK_input(CLK_input), .Reset(or_1_out), .out_put(st_hr));
  add_4_bits add_4_bits_2 (.enable(or_4_out), .CLK_input(CLK_input), .Reset(or_3_out), .out_put(wk_hr));
  reset_conditions reset_conditions_1 (
    .bit_4_wk(wk_hr[3]), .bit_3_wk(wk_hr[2]), .bit_2_wk(wk_hr[1]), .bit_1_wk(wk_hr[0]), .bit_2_st(st_hr[1]),
    .bit_1_st(st_hr[0]), .reset_impulse(reset_impulse));
  or or_5 (reset, and_4_out, and_5_out, and_6_out);
  and and_3 (out_7, st_hr[0], st_hr[1]);
  and and_4 (and_4_out, wk_hr[2], st_hr[1]);
  and and_5 (and_5_out, st_hr[1], st_hr[0], wk_hr[3]);
  and and_6 (and_6_out, st_hr[1], wk_hr[0], wk_hr[2]);
  and and_7 (out_6, wk_hr[1], wk_hr[3]);
  and and_8 (c_out, st_hr[1], c_in_m, and_9_out, c_in_s);
  and and_9 (and_9_out, wk_hr[1], wk_hr[0]);
  and and_10 (incr_1, wk_hr[3], wk_hr[1]);
  and and_11 (incr_2, wk_hr[0], wk_hr[3]);
endmodule

module add_4_bits (
  input  enable,
  input  CLK_input,
  input  Reset,
  output [3:0] out_put
);

  wire and_1_out, and_2_out, and_3_out, and_4_out, and_5_out;

  J_K_Flip_Flop j_k_ff_1 (.J(enable), .K(enable), .clk(CLK_input), .Q(out_put[0]), .reset(Reset));  // open: Qn, preset
  J_K_Flip_Flop j_k_ff_2 (
    .J(and_1_out), .K(and_1_out), .clk(CLK_input), .Q(out_put[1]), .reset(Reset));  // open: Qn, preset
  and and_1 (and_1_out, enable, out_put[0]);
  and and_2 (and_2_out, out_put[1], out_put[0]);
  and and_3 (and_3_out, enable, and_2_out);
  J_K_Flip_Flop j_k_ff_3 (
    .J(and_3_out), .K(and_3_out), .clk(CLK_input), .Q(out_put[2]), .reset(Reset));  // open: Qn, preset
  and and_4 (and_4_out, and_2_out, out_put[2]);
  J_K_Flip_Flop j_k_ff_4 (
    .J(and_5_out), .K(and_5_out), .clk(CLK_input), .Q(out_put[3]), .reset(Reset));  // open: Qn, preset
  and and_5 (and_5_out, enable, and_4_out);

  // Other names for the same wires on the sheet: EN = enable
endmodule

module mid_letter (
  input  [3:0] month_num,
  output cnt,
  output lft_high,
  output top,
  output right_h,
  output left_bt,
  output bt,
  output right_bt
);

  wire and_1_out, and_2_out, and_3_out, and_4_out, and_5_out, and_6_out, and_7_out, and_8_out, and_9_out,
       and_10_out, and_11_out, and_12_out, and_13_out, and_14_out, and_15_out, and_16_out, and_17_out,
       and_18_out, and_19_out, and_20_out, and_21_out, and_22_out, and_23_out, and_24_out, and_25_out,
       and_26_out, and_27_out, and_28_out, not_1_out, not_2_out, not_3_out, not_4_out, not_5_out, not_6_out,
       not_7_out, not_8_out, not_9_out, not_10_out, not_11_out, not_12_out, not_13_out, not_14_out,
       not_15_out, not_16_out, not_17_out, not_18_out, not_19_out, not_20_out, not_21_out, not_22_out,
       not_23_out, not_24_out, not_25_out, not_26_out, not_27_out, not_28_out, not_29_out, not_30_out,
       not_31_out, not_32_out, not_33_out, not_34_out, not_35_out, not_36_out, not_37_out;

  not not_1 (not_1_out, month_num[1]);
  not not_2 (not_2_out, month_num[3]);
  not not_3 (not_3_out, month_num[2]);
  not not_4 (not_4_out, month_num[1]);
  not not_5 (not_5_out, month_num[3]);
  not not_6 (not_6_out, month_num[3]);
  not not_7 (not_7_out, month_num[3]);
  not not_8 (not_8_out, month_num[2]);
  not not_9 (not_9_out, month_num[1]);
  not not_10 (not_10_out, month_num[0]);
  not not_11 (not_11_out, month_num[1]);
  not not_12 (not_12_out, month_num[2]);
  not not_13 (not_13_out, month_num[1]);
  not not_14 (not_14_out, month_num[3]);
  not not_15 (not_15_out, month_num[2]);
  not not_16 (not_16_out, month_num[3]);
  not not_17 (not_17_out, month_num[2]);
  not not_18 (not_18_out, month_num[1]);
  not not_19 (not_19_out, month_num[0]);
  not not_20 (not_20_out, month_num[3]);
  not not_21 (not_21_out, month_num[3]);
  not not_22 (not_22_out, month_num[3]);
  not not_23 (not_23_out, month_num[2]);
  not not_24 (not_24_out, month_num[1]);
  not not_25 (not_25_out, month_num[0]);
  not not_26 (not_26_out, month_num[3]);
  not not_27 (not_27_out, month_num[0]);
  not not_28 (not_28_out, month_num[1]);
  not not_29 (not_29_out, month_num[0]);
  not not_30 (not_30_out, month_num[3]);
  not not_31 (not_31_out, month_num[2]);
  not not_32 (not_32_out, month_num[3]);
  not not_33 (not_33_out, month_num[2]);
  not not_34 (not_34_out, month_num[3]);
  not not_35 (not_35_out, month_num[2]);
  not not_36 (not_36_out, month_num[1]);
  not not_37 (not_37_out, month_num[0]);
  and and_1 (and_1_out, not_1_out, month_num[0]);
  and and_2 (and_2_out, not_2_out, not_3_out, month_num[1]);
  and and_3 (and_3_out, month_num[3], month_num[2], not_4_out);
  and and_4 (and_4_out, not_5_out, month_num[0]);
  and and_5 (and_5_out, not_6_out, month_num[1]);
  and and_6 (and_6_out, not_7_out, month_num[2]);
  and and_7 (and_7_out, month_num[3], not_8_out);
  and and_8 (and_8_out, month_num[3], not_9_out, not_10_out);
  and and_9 (and_9_out, not_11_out, month_num[0]);
  and and_10 (and_10_out, not_12_out, month_num[1]);
  and and_11 (and_11_out, month_num[3], month_num[2], not_13_out);
  and and_12 (and_12_out, not_14_out, month_num[0]);
  and and_13 (and_13_out, not_15_out, month_num[1], month_num[0]);
  and and_14 (and_14_out, not_16_out, month_num[2]);
  and and_15 (and_15_out, month_num[3], not_17_out, not_18_out, not_19_out);
  and and_16 (and_16_out, not_20_out, month_num[0]);
  and and_17 (and_17_out, not_21_out, month_num[1]);
  and and_18 (and_18_out, not_22_out, month_num[2]);
  and and_19 (and_19_out, month_num[3], not_23_out);
  and and_20 (and_20_out, month_num[3], not_24_out, not_25_out);
  and and_21 (and_21_out, not_26_out, month_num[1], not_27_out);
  and and_22 (and_22_out, month_num[2], not_28_out, not_29_out);
  and and_23 (and_23_out, not_30_out, month_num[2], month_num[1]);
  and and_24 (and_24_out, month_num[3], not_31_out);
  and and_25 (and_25_out, not_32_out, month_num[0]);
  and and_26 (and_26_out, not_33_out, month_num[1], month_num[0]);
  and and_27 (and_27_out, not_34_out, month_num[2]);
  and and_28 (and_28_out, month_num[3], not_35_out, not_36_out, not_37_out);
  or or_1 (cnt, and_1_out, and_2_out, and_3_out);
  or or_2 (lft_high, and_4_out, and_5_out, and_6_out, and_7_out, and_8_out);
  or or_3 (top, and_9_out, and_10_out, and_11_out);
  or or_4 (right_h, and_12_out, and_13_out, and_14_out, and_15_out);
  or or_5 (left_bt, and_16_out, and_17_out, and_18_out, and_19_out, and_20_out);
  or or_6 (bt, and_21_out, and_22_out, and_23_out, and_24_out);
  or or_7 (right_bt, and_25_out, and_26_out, and_27_out, and_28_out);
endmodule

module fst_letter (
  input  [3:0] month_num,
  output cnt,
  output left_h,
  output top,
  output right_h,
  output left_bt,
  output bt,
  output right_bt
);

  wire and_1_out, and_2_out, and_3_out, and_4_out, and_5_out, and_6_out, and_7_out, and_8_out, and_9_out,
       and_10_out, and_11_out, and_12_out, and_13_out, and_14_out, and_15_out, and_16_out, and_17_out,
       and_18_out, and_19_out, and_20_out, and_21_out, and_22_out, and_23_out, and_24_out, and_25_out,
       and_26_out, and_27_out, not_1_out, not_2_out, not_3_out, not_4_out, not_5_out, not_6_out, not_7_out,
       not_8_out, not_9_out, not_10_out, not_11_out, not_12_out, not_13_out, not_14_out, not_15_out,
       not_16_out, not_17_out, not_18_out, not_19_out, not_20_out, not_21_out, not_22_out, not_23_out,
       not_24_out, not_25_out, not_26_out, not_27_out, not_28_out, not_29_out, not_30_out, not_31_out,
       not_32_out, not_33_out, not_34_out, not_35_out, not_36_out, not_37_out, not_38_out, not_39_out,
       not_40_out, not_41_out, not_42_out, not_43_out, not_44_out, not_45_out, not_46_out, not_47_out;

  not not_1 (not_1_out, month_num[3]);
  not not_2 (not_2_out, month_num[2]);
  not not_3 (not_3_out, month_num[0]);
  not not_4 (not_4_out, month_num[1]);
  not not_5 (not_5_out, month_num[0]);
  not not_6 (not_6_out, month_num[2]);
  not not_7 (not_7_out, month_num[1]);
  not not_8 (not_8_out, month_num[2]);
  not not_9 (not_9_out, month_num[3]);
  not not_10 (not_10_out, month_num[2]);
  and and_1 (and_1_out, not_9_out, not_10_out, month_num[1]);
  not not_11 (not_11_out, month_num[3]);
  and and_2 (and_2_out, not_11_out, month_num[2], not_12_out);
  not not_12 (not_12_out, month_num[1]);
  and and_3 (and_3_out, month_num[3], not_13_out, not_14_out);
  not not_13 (not_13_out, month_num[2]);
  not not_14 (not_14_out, month_num[1]);
  not not_15 (not_15_out, month_num[2]);
  and and_4 (and_4_out, month_num[3], not_15_out, not_16_out);
  not not_16 (not_16_out, month_num[0]);
  not not_17 (not_17_out, month_num[3]);
  not not_18 (not_18_out, month_num[2]);
  and and_5 (and_5_out, not_17_out, not_18_out, month_num[1]);
  not not_19 (not_19_out, month_num[3]);
  and and_6 (and_6_out, not_19_out, month_num[2], not_20_out);
  not not_20 (not_20_out, month_num[1]);
  not not_21 (not_21_out, month_num[2]);
  and and_7 (and_7_out, month_num[3], not_21_out, not_22_out);
  not not_22 (not_22_out, month_num[1]);
  and and_8 (and_8_out, month_num[3], not_23_out, not_24_out);
  not not_23 (not_23_out, month_num[2]);
  not not_24 (not_24_out, month_num[0]);
  not not_25 (not_25_out, month_num[3]);
  and and_9 (and_9_out, not_25_out, month_num[0]);
  not not_26 (not_26_out, month_num[3]);
  and and_10 (and_10_out, not_26_out, month_num[2]);
  and and_11 (and_11_out, month_num[3], not_27_out, not_28_out);
  not not_27 (not_27_out, month_num[2]);
  not not_28 (not_28_out, month_num[0]);
  and and_12 (and_12_out, month_num[3], not_29_out, not_30_out);
  not not_29 (not_29_out, month_num[1]);
  not not_30 (not_30_out, month_num[0]);
  not not_31 (not_31_out, month_num[2]);
  and and_13 (and_13_out, not_31_out, month_num[1]);
  not not_32 (not_32_out, month_num[3]);
  and and_14 (and_14_out, not_32_out, month_num[2], not_33_out);
  not not_33 (not_33_out, month_num[1]);
  and and_15 (and_15_out, month_num[3], not_34_out, not_35_out);
  not not_34 (not_34_out, month_num[1]);
  not not_35 (not_35_out, month_num[0]);
  not not_36 (not_36_out, month_num[2]);
  not not_37 (not_37_out, month_num[1]);
  not not_38 (not_38_out, month_num[3]);
  not not_39 (not_39_out, month_num[2]);
  not not_40 (not_40_out, month_num[0]);
  not not_41 (not_41_out, month_num[1]);
  not not_42 (not_42_out, month_num[0]);
  not not_43 (not_43_out, month_num[3]);
  and and_16 (and_16_out, not_43_out, month_num[0]);
  not not_44 (not_44_out, month_num[3]);
  and and_17 (and_17_out, not_44_out, month_num[2]);
  and and_18 (and_18_out, month_num[3], not_45_out);
  not not_45 (not_45_out, month_num[2]);
  and and_19 (and_19_out, month_num[3], not_46_out, not_47_out);
  not not_46 (not_46_out, month_num[1]);
  not not_47 (not_47_out, month_num[0]);
  and and_20 (and_20_out, not_1_out, not_2_out, month_num[1], not_3_out);
  and and_21 (and_21_out, month_num[2], not_4_out, not_5_out);
  and and_22 (and_22_out, month_num[3], not_6_out, not_7_out);
  and and_23 (and_23_out, month_num[3], not_8_out, month_num[0]);
  or or_1 (left_h, and_1_out, and_2_out, and_3_out, and_4_out);
  or or_2 (top, and_5_out, and_6_out, and_7_out, and_8_out);
  or or_3 (right_h, and_9_out, and_10_out, and_11_out, and_12_out);
  or or_4 (left_bt, and_13_out, and_14_out, and_15_out);
  and and_24 (and_24_out, not_36_out, not_37_out, month_num[0]);
  and and_25 (and_25_out, not_38_out, month_num[2], month_num[1]);
  and and_26 (and_26_out, month_num[3], not_39_out, month_num[1], not_40_out);
  and and_27 (and_27_out, month_num[3], month_num[2], not_41_out, not_42_out);
  or or_5 (right_bt, and_16_out, and_17_out, and_18_out, and_19_out);
  or or_6 (cnt, and_20_out, and_21_out, and_22_out, and_23_out);
  or or_7 (bt, and_24_out, and_25_out, and_26_out, and_27_out);
endmodule

module thd_letter (
  input  [3:0] month_num,
  output cnt,
  output left_h,
  output top,
  output right_h,
  output left_bottom,
  output bt,
  output right_bt
);

  wire and_1_out, and_2_out, and_3_out, and_4_out, and_5_out, and_6_out, and_7_out, and_8_out, and_9_out,
       and_10_out, and_11_out, and_12_out, and_13_out, and_14_out, and_15_out, and_16_out, and_17_out,
       and_18_out, and_19_out, and_20_out, and_21_out, and_22_out, and_23_out, and_24_out, and_25_out,
       not_1_out, not_2_out, not_3_out, not_4_out, not_5_out, not_6_out, not_7_out, not_8_out, not_9_out,
       not_10_out, not_11_out, not_12_out, not_13_out, not_14_out, not_15_out, not_16_out, not_17_out,
       not_18_out, not_19_out, not_20_out, not_21_out, not_22_out, not_23_out, not_24_out, not_25_out,
       not_26_out, not_27_out, not_28_out, not_29_out, not_30_out, not_31_out, not_32_out, not_33_out,
       not_34_out, not_35_out, not_36_out, not_37_out, not_38_out, not_39_out, not_40_out;

  not not_1 (not_1_out, month_num[1]);
  not not_2 (not_2_out, month_num[3]);
  not not_3 (not_3_out, month_num[0]);
  not not_4 (not_4_out, month_num[2]);
  not not_5 (not_5_out, month_num[0]);
  not not_6 (not_6_out, month_num[2]);
  not not_7 (not_7_out, month_num[3]);
  not not_8 (not_8_out, month_num[1]);
  not not_9 (not_9_out, month_num[3]);
  not not_10 (not_10_out, month_num[2]);
  not not_11 (not_11_out, month_num[1]);
  not not_12 (not_12_out, month_num[0]);
  not not_13 (not_13_out, month_num[3]);
  not not_14 (not_14_out, month_num[2]);
  not not_15 (not_15_out, month_num[1]);
  not not_16 (not_16_out, month_num[0]);
  not not_17 (not_17_out, month_num[2]);
  not not_18 (not_18_out, month_num[1]);
  not not_19 (not_19_out, month_num[3]);
  not not_20 (not_20_out, month_num[1]);
  not not_21 (not_21_out, month_num[2]);
  not not_22 (not_22_out, month_num[2]);
  not not_23 (not_23_out, month_num[3]);
  not not_24 (not_24_out, month_num[1]);
  not not_25 (not_25_out, month_num[0]);
  not not_26 (not_26_out, month_num[2]);
  not not_27 (not_27_out, month_num[2]);
  not not_28 (not_28_out, month_num[0]);
  not not_29 (not_29_out, month_num[3]);
  not not_30 (not_30_out, month_num[1]);
  not not_31 (not_31_out, month_num[0]);
  not not_32 (not_32_out, month_num[2]);
  not not_33 (not_33_out, month_num[3]);
  not not_34 (not_34_out, month_num[1]);
  not not_35 (not_35_out, month_num[3]);
  not not_36 (not_36_out, month_num[0]);
  not not_37 (not_37_out, month_num[2]);
  not not_38 (not_38_out, month_num[1]);
  not not_39 (not_39_out, month_num[0]);
  not not_40 (not_40_out, month_num[2]);
  and and_1 (and_1_out, not_1_out, month_num[0]);
  or or_1 (cnt, and_1_out, and_2_out, and_3_out);
  and and_2 (and_2_out, not_2_out, month_num[1], not_3_out);
  and and_3 (and_3_out, month_num[3], not_4_out, not_5_out);
  and and_4 (and_4_out, not_6_out, month_num[1]);
  and and_5 (and_5_out, not_7_out, month_num[2], not_8_out);
  and and_6 (and_6_out, not_9_out, month_num[2], month_num[0]);
  and and_7 (and_7_out, month_num[3], not_10_out);
  and and_8 (and_8_out, month_num[3], not_11_out, not_12_out);
  and and_9 (and_9_out, not_13_out, not_14_out, month_num[1], month_num[0]);
  and and_10 (and_10_out, month_num[2], not_15_out, not_16_out);
  and and_11 (and_11_out, month_num[3], not_17_out, not_18_out);
  and and_12 (and_12_out, not_19_out, month_num[2], not_20_out, month_num[0]);
  and and_13 (and_13_out, month_num[3], not_21_out, month_num[0]);
  and and_14 (and_14_out, not_22_out, month_num[0]);
  and and_15 (and_15_out, not_23_out, month_num[1]);
  and and_16 (and_16_out, month_num[2], not_24_out, not_25_out);
  and and_17 (and_17_out, month_num[3], not_26_out);
  and and_18 (and_18_out, not_27_out, month_num[1], not_28_out);
  and and_19 (and_19_out, not_29_out, month_num[2], month_num[0]);
  and and_20 (and_20_out, month_num[3], not_30_out, not_31_out);
  and and_21 (and_21_out, month_num[3], not_32_out, month_num[1]);
  and and_22 (and_22_out, not_33_out, not_34_out, month_num[0]);
  and and_23 (and_23_out, not_35_out, month_num[1], not_36_out);
  and and_24 (and_24_out, month_num[3], not_37_out, not_38_out, not_39_out);
  and and_25 (and_25_out, month_num[3], not_40_out, month_num[1], month_num[0]);
  or or_2 (left_h, and_4_out, and_5_out, and_6_out, and_7_out, and_8_out);
  or or_3 (top, and_9_out, and_10_out, and_11_out);
  or or_4 (right_h, and_12_out, and_13_out);
  or or_5 (left_bottom, and_14_out, and_15_out, and_16_out, and_17_out);
  or or_6 (bt, and_18_out, and_19_out, and_20_out, and_21_out);
  or or_7 (right_bt, and_22_out, and_23_out, and_24_out, and_25_out);
endmodule

module date (
  input  enable,
  input  CLK_input,
  output [3:0] Low_day,
  output [3:0] High_day,
  output [3:0] month_numerical_value
);

  wire and_4_out, and_7_out, and_8_out, en_j2, en_m2, fixer, month_lgth_1_f, not_1_out, not_2_out, not_3_out,
       not_4_out, not_5_out, or_1_out, or_2_out, or_3_out, reset_30, rs_j1, rs_j2, rs_j2_p;

  or or_1 (or_1_out, rs_j1, rs_j2, reset_30);
  or or_2 (or_2_out, rs_j2, reset_30, rs_j2_p);
  or or_3 (or_3_out, en_m2, and_4_out);
  add_4_bits add_4_bits_1 (.enable(enable), .CLK_input(CLK_input), .Reset(or_1_out), .out_put(Low_day));
  add_4_bits add_4_bits_2 (.enable(en_j2), .CLK_input(CLK_input), .Reset(or_2_out), .out_put(High_day));
  add_4_bits add_4_bits_3 (.enable(or_3_out), .CLK_input(CLK_input), .Reset(1'b0), .out_put(month_numerical_value));
  and and_1 (en_j2, Low_day[0], Low_day[3]);
  and and_2 (rs_j1, Low_day[1], Low_day[3]);
  not not_1 (not_1_out, Low_day[3]);
  and and_3 (fixer, High_day[0], High_day[1]);
  and and_4 (and_4_out, ~month_numerical_value[0], ~month_numerical_value[1], ~month_numerical_value[2], ~month_numerical_value[3]);  // AND_Gate
  and cl_31 (rs_j2, Low_day[1], not_1_out, fixer);
  not not_2 (not_2_out, month_lgth_1_f);
  month_lgth month_lgth_1 (
    .A(month_numerical_value[0]), .B(month_numerical_value[1]), .C(month_numerical_value[2]),
    .D(month_numerical_value[3]), .f(month_lgth_1_f));
  and and_5 (rs_j2_p, Low_day[0], fixer, not_2_out);
  not not_3 (not_3_out, month_lgth_1_f);
  and and_6 (reset_30, not_3_out, fixer, Low_day[0]);
  not not_4 (not_4_out, Low_day[0]);
  not not_5 (not_5_out, month_lgth_1_f);
  and and_7 (and_7_out, Low_day[0], fixer, month_lgth_1_f);
  and and_8 (and_8_out, fixer, not_4_out, not_5_out);
  or or_4 (en_m2, and_8_out, and_7_out);

  // Other names for the same wires on the sheet: CLK = CLK_input; en_m1 = Low_day[0]; one_j1 = Low_day[0]
endmodule

module month_lgth (
  input  A,
  input  B,
  input  C,
  input  D,
  output f
);

  wire and_1_out, and_2_out, and_3_out, not_1_out, not_2_out;

  not not_1 (not_1_out, A);
  and and_1 (and_1_out, not_1_out, not_2_out);
  not not_2 (not_2_out, D);
  and and_2 (and_2_out, B, C);
  and and_3 (and_3_out, A, D);
  or or_1 (f, and_1_out, and_2_out, and_3_out);
endmodule

module hours_conditions (
  input  [3:0] wk_hours_input,
  input  [3:0] st_hours_input,
  output reset_impulse
);

  wire and_1_out, and_2_out, and_3_out, and_4_out, and_5_out, and_6_out, and_7_out, and_8_out, not_1_out,
       not_2_out, not_3_out, not_4_out, not_5_out, not_6_out, not_7_out, not_8_out, not_9_out, not_10_out,
       not_11_out, not_12_out, not_14_out, not_15_out;

  not not_1 (not_1_out, wk_hours_input[2]);
  not not_2 (not_2_out, wk_hours_input[3]);
  not not_3 (not_3_out, wk_hours_input[0]);
  not not_4 (not_4_out, wk_hours_input[2]);
  not not_5 (not_5_out, wk_hours_input[3]);
  not not_6 (not_6_out, wk_hours_input[2]);
  not not_7 (not_7_out, wk_hours_input[2]);
  not not_8 (not_8_out, wk_hours_input[0]);
  not not_9 (not_9_out, wk_hours_input[1]);
  and and_1 (and_1_out, not_8_out, not_9_out, not_10_out, not_11_out);
  not not_10 (not_10_out, wk_hours_input[2]);
  not not_11 (not_11_out, wk_hours_input[2]);
  not not_12 (not_12_out, wk_hours_input[0]);
  not not_13 (not_12_out, wk_hours_input[1]);
  and and_2 (and_2_out, not_12_out, not_12_out, not_1_out, not_2_out);
  and and_3 (and_3_out, wk_hours_input[1], not_3_out, not_4_out, not_5_out);
  and and_4 (and_4_out, wk_hours_input[0], wk_hours_input[1], not_6_out, not_7_out);
  not not_14 (not_14_out, and_2_out);
  and and_5 (and_5_out, not_14_out, st_hours_input[1]);
  not not_15 (not_15_out, and_3_out);
  and and_6 (and_6_out, not_15_out, st_hours_input[1]);
  and and_7 (and_7_out, and_4_out, st_hours_input[1]);
  and and_8 (and_8_out, and_1_out, st_hours_input[1]);
  or or_1 (reset_impulse, and_5_out, and_6_out, and_7_out, and_8_out);

  assign {st_hours_input[2], st_hours_input[0]} = {2{st_hours_input[3]}};
  // also tied to GND on the sheet: st_hours_input[3]

  // Other names for the same wires on the sheet: one = wk_hours_input[0]; two = wk_hours_input[1];
  //   four = wk_hours_input[2]; three = wk_hours_input[2]
endmodule

module format_convert (
  input  [3:0] wk_hr_input,
  input  [3:0] st_hr_input,
  output hour_one,
  output hour_two,
  output hour_four,
  output hour_eight,
  output strong_one
);

  wire and_1_out, and_2_out, and_3_out, and_4_out, and_5_out, and_6_out, and_7_out, and_8_out, and_9_out,
       and_10_out, and_11_out, and_12_out, and_13_out, and_14_out, and_15_out, and_16_out, not_1_out,
       not_2_out, not_3_out, not_4_out, not_5_out, not_6_out, not_7_out, not_8_out, not_9_out, not_10_out,
       not_11_out, not_12_out, not_13_out, not_14_out, not_15_out, not_16_out, not_17_out, not_18_out,
       not_19_out, not_20_out, not_21_out, not_22_out, not_23_out, not_24_out, not_25_out, not_26_out,
       not_27_out, not_28_out, not_29_out, not_30_out, not_31_out, not_32_out, not_33_out, not_34_out,
       not_35_out, not_36_out, not_37_out, not_38_out, not_39_out, not_40_out, not_41_out, not_42_out,
       not_43_out, not_44_out, not_45_out, not_46_out, not_47_out, not_48_out, not_49_out, not_50_out,
       not_51_out, not_52_out;

  not not_1 (not_1_out, wk_hr_input[3]);
  not not_2 (not_2_out, wk_hr_input[2]);
  not not_3 (not_3_out, st_hr_input[0]);
  not not_4 (not_4_out, wk_hr_input[3]);
  not not_5 (not_5_out, st_hr_input[1]);
  not not_6 (not_6_out, wk_hr_input[2]);
  not not_7 (not_7_out, wk_hr_input[1]);
  not not_8 (not_8_out, st_hr_input[1]);
  not not_9 (not_9_out, wk_hr_input[3]);
  not not_10 (not_10_out, st_hr_input[1]);
  not not_11 (not_11_out, st_hr_input[0]);
  not not_12 (not_12_out, wk_hr_input[2]);
  not not_13 (not_13_out, wk_hr_input[0]);
  not not_14 (not_14_out, st_hr_input[1]);
  not not_15 (not_15_out, st_hr_input[0]);
  not not_16 (not_16_out, wk_hr_input[3]);
  not not_17 (not_17_out, wk_hr_input[1]);
  not not_18 (not_18_out, st_hr_input[1]);
  not not_19 (not_19_out, wk_hr_input[3]);
  not not_20 (not_20_out, wk_hr_input[1]);
  not not_21 (not_21_out, wk_hr_input[0]);
  not not_22 (not_22_out, st_hr_input[0]);
  not not_23 (not_23_out, wk_hr_input[2]);
  not not_24 (not_24_out, wk_hr_input[1]);
  not not_25 (not_25_out, st_hr_input[1]);
  not not_26 (not_26_out, wk_hr_input[3]);
  not not_27 (not_27_out, st_hr_input[1]);
  not not_28 (not_28_out, st_hr_input[0]);
  not not_29 (not_29_out, wk_hr_input[3]);
  not not_30 (not_30_out, st_hr_input[1]);
  not not_31 (not_31_out, wk_hr_input[2]);
  not not_32 (not_32_out, wk_hr_input[1]);
  not not_33 (not_33_out, st_hr_input[1]);
  not not_34 (not_34_out, wk_hr_input[3]);
  not not_35 (not_35_out, wk_hr_input[2]);
  not not_36 (not_36_out, wk_hr_input[1]);
  not not_37 (not_37_out, st_hr_input[0]);
  not not_38 (not_38_out, wk_hr_input[2]);
  not not_39 (not_39_out, wk_hr_input[1]);
  not not_40 (not_40_out, st_hr_input[1]);
  not not_41 (not_41_out, st_hr_input[0]);
  not not_42 (not_42_out, wk_hr_input[2]);
  not not_43 (not_43_out, wk_hr_input[0]);
  not not_44 (not_44_out, st_hr_input[1]);
  not not_45 (not_45_out, st_hr_input[0]);
  not not_46 (not_46_out, wk_hr_input[3]);
  not not_47 (not_47_out, wk_hr_input[2]);
  not not_48 (not_48_out, wk_hr_input[1]);
  not not_49 (not_49_out, st_hr_input[1]);
  not not_50 (not_50_out, wk_hr_input[3]);
  not not_51 (not_51_out, wk_hr_input[2]);
  not not_52 (not_52_out, st_hr_input[0]);
  and and_1 (and_1_out, not_1_out, not_2_out, wk_hr_input[0], not_3_out);
  and and_2 (and_2_out, not_4_out, wk_hr_input[0], not_5_out);
  and and_3 (and_3_out, not_6_out, not_7_out, wk_hr_input[0], not_8_out);
  and and_4 (and_4_out, not_9_out, wk_hr_input[1], not_10_out, not_11_out);
  and and_5 (and_5_out, not_12_out, wk_hr_input[1], not_13_out, not_14_out, not_15_out);
  and and_6 (and_6_out, not_16_out, wk_hr_input[2], not_17_out, not_18_out, st_hr_input[0]);
  and and_7 (and_7_out, not_19_out, wk_hr_input[2], not_20_out, not_21_out, st_hr_input[1], not_22_out);
  and and_8 (and_8_out, wk_hr_input[3], not_23_out, not_24_out, not_25_out, st_hr_input[0]);
  and and_9 (and_9_out, not_26_out, wk_hr_input[2], not_27_out, not_28_out);
  and and_10 (and_10_out, not_29_out, wk_hr_input[2], wk_hr_input[1], not_30_out);
  and and_11 (and_11_out, wk_hr_input[3], not_31_out, not_32_out, not_33_out, st_hr_input[0]);
  and and_12 (and_12_out, not_34_out, not_35_out, not_36_out, st_hr_input[1], not_37_out);
  and and_13 (and_13_out, wk_hr_input[3], not_38_out, not_39_out, not_40_out, not_41_out);
  and and_14 (and_14_out, wk_hr_input[3], not_42_out, not_43_out, not_44_out, not_45_out);
  and and_15 (and_15_out, not_46_out, not_47_out, not_48_out, not_49_out, st_hr_input[0]);
  and and_16 (and_16_out, not_50_out, not_51_out, wk_hr_input[1], st_hr_input[1], not_52_out);
  or or_1 (hour_one, and_1_out, and_2_out, and_3_out);
  or or_2 (hour_two, and_4_out, and_5_out, and_6_out, and_7_out, and_8_out);
  or or_3 (hour_four, and_9_out, and_10_out, and_11_out);
  or or_4 (hour_eight, and_12_out, and_13_out, and_14_out);
  or or_5 (strong_one, and_15_out, and_16_out);
endmodule

module reset_conditions (
  input  bit_4_wk,
  input  bit_3_wk,
  input  bit_2_wk,
  input  bit_1_wk,
  input  bit_2_st,
  input  bit_1_st,
  output reset_impulse
);

  wire and_1_out, and_2_out, and_3_out, and_4_out, not_1_out, not_2_out, not_3_out, not_4_out, not_5_out,
       not_6_out, not_7_out, not_8_out, not_9_out;

  not not_1 (not_1_out, bit_4_wk);
  not not_2 (not_2_out, bit_1_st);
  not not_3 (not_3_out, bit_4_wk);
  not not_4 (not_4_out, bit_1_st);
  not not_5 (not_5_out, bit_3_wk);
  not not_6 (not_6_out, bit_2_wk);
  not not_7 (not_7_out, bit_1_st);
  not not_8 (not_8_out, bit_3_wk);
  not not_9 (not_9_out, bit_1_st);
  and and_1 (and_1_out, not_1_out, bit_3_wk, bit_1_wk, bit_2_st, not_2_out);
  and and_2 (and_2_out, not_3_out, bit_3_wk, bit_2_wk, bit_2_st, not_4_out);
  and and_3 (and_3_out, bit_4_wk, not_5_out, not_6_out, bit_2_st, not_7_out);
  and and_4 (and_4_out, bit_4_wk, not_8_out, bit_1_wk, bit_2_st, not_9_out);
  or or_1 (reset_impulse, and_1_out, and_2_out, and_3_out, and_4_out);
endmodule

module count_512_t (
  input  EN,
  input  R,
  output c
);

  wire and_1_out, and_2_out, and_3_out, and_4_out, and_5_out, and_6_out, and_7_out, and_8_out, and_9_out,
       and_10_out, and_11_out, and_12_out, and_13_out, and_14_out, and_15_out, clock_1_out, t_ff_1_q,
       t_ff_2_q, t_ff_3_q, t_ff_4_q, t_ff_5_q, t_ff_6_q, t_ff_7_q, t_ff_8_q, t_ff_9_q;

  Clock clock_1 (.out(clock_1_out));
  and and_1 (and_1_out, t_ff_1_q, EN);
  and and_2 (and_2_out, and_9_out, EN);
  and and_3 (and_3_out, and_10_out, EN);
  and and_4 (and_4_out, and_11_out, EN);
  and and_5 (and_5_out, and_12_out, EN);
  and and_6 (and_6_out, and_13_out, EN);
  and and_7 (and_7_out, and_14_out, EN);
  and and_8 (and_8_out, and_15_out, EN);
  T_Flip_Flop t_ff_1 (.T(EN), .clk(clock_1_out), .Q(t_ff_1_q), .reset(R));  // open: Qn, preset
  T_Flip_Flop t_ff_2 (.T(and_1_out), .clk(clock_1_out), .Q(t_ff_2_q), .reset(R));  // open: Qn, preset
  T_Flip_Flop t_ff_3 (.T(and_2_out), .clk(clock_1_out), .Q(t_ff_3_q), .reset(R));  // open: Qn, preset
  T_Flip_Flop t_ff_4 (.T(and_3_out), .clk(clock_1_out), .Q(t_ff_4_q), .reset(R));  // open: Qn, preset
  T_Flip_Flop t_ff_5 (.T(and_4_out), .clk(clock_1_out), .Q(t_ff_5_q), .reset(R));  // open: Qn, preset
  T_Flip_Flop t_ff_6 (.T(and_5_out), .clk(clock_1_out), .Q(t_ff_6_q), .reset(R));  // open: Qn, preset
  T_Flip_Flop t_ff_7 (.T(and_6_out), .clk(clock_1_out), .Q(t_ff_7_q), .reset(R));  // open: Qn, preset
  T_Flip_Flop t_ff_8 (.T(and_7_out), .clk(clock_1_out), .Q(t_ff_8_q), .reset(R));  // open: Qn, preset
  T_Flip_Flop t_ff_9 (.T(and_8_out), .clk(clock_1_out), .Q(t_ff_9_q), .reset(R));  // open: Qn, preset
  and and_9 (and_9_out, t_ff_2_q, t_ff_1_q);
  and and_10 (and_10_out, t_ff_3_q, and_9_out);
  and and_11 (and_11_out, t_ff_4_q, and_10_out);
  and and_12 (and_12_out, t_ff_5_q, and_11_out);
  and and_13 (and_13_out, t_ff_6_q, and_12_out);
  and and_14 (and_14_out, t_ff_7_q, and_13_out);
  and and_15 (and_15_out, t_ff_8_q, and_14_out);
  and and_16 (c, t_ff_9_q, and_15_out, and_14_out, and_13_out, and_12_out, and_11_out, and_10_out, and_9_out, t_ff_1_q);

  // Notes on the sheet:
  //   count to 100 - used for 1024Hz input
endmodule

module count_100_t (
  input  EN,
  input  R,
  output Output_1
);

  wire and_1_out, and_2_out, and_3_out, and_4_out, and_5_out, and_6_out, and_7_out, and_8_out, and_9_out,
       and_10_out, and_11_out, and_12_out, and_13_out, clock_1_out, j_k_ff_1_q, j_k_ff_2_q, j_k_ff_3_q,
       j_k_ff_4_q, j_k_ff_5_q, j_k_ff_6_q, j_k_ff_7_q, or_1_out;

  Clock clock_1 (.out(clock_1_out));
  J_K_Flip_Flop j_k_ff_1 (
    .J(EN), .K(EN), .clk(clock_1_out), .Q(j_k_ff_1_q), .preset(1'b0), .reset(or_1_out));  // open: Qn
  and and_1 (and_1_out, j_k_ff_1_q, and_13_out);
  or or_1 (or_1_out, R, and_1_out);
  and and_2 (and_2_out, EN, j_k_ff_1_q);
  J_K_Flip_Flop j_k_ff_2 (
    .J(and_2_out), .K(and_2_out), .clk(clock_1_out), .Q(j_k_ff_2_q), .preset(1'b0), .reset(or_1_out));  // open: Qn
  and and_3 (and_3_out, j_k_ff_2_q, j_k_ff_1_q);
  and and_4 (and_4_out, EN, and_3_out);
  J_K_Flip_Flop j_k_ff_3 (
    .J(and_4_out), .K(and_4_out), .clk(clock_1_out), .Q(j_k_ff_3_q), .preset(1'b0), .reset(or_1_out));  // open: Qn
  and and_5 (and_5_out, and_3_out, j_k_ff_3_q);
  J_K_Flip_Flop j_k_ff_4 (
    .J(and_6_out), .K(and_6_out), .clk(clock_1_out), .Q(j_k_ff_4_q), .preset(1'b0), .reset(or_1_out));  // open: Qn
  and and_6 (and_6_out, EN, and_5_out);
  and and_7 (and_7_out, and_5_out, j_k_ff_4_q);
  J_K_Flip_Flop j_k_ff_5 (
    .J(and_8_out), .K(and_8_out), .clk(clock_1_out), .Q(j_k_ff_5_q), .preset(1'b0), .reset(or_1_out));  // open: Qn
  and and_8 (and_8_out, EN, and_7_out);
  and and_9 (and_9_out, and_7_out, j_k_ff_5_q);
  and and_10 (and_10_out, EN, and_9_out);
  J_K_Flip_Flop j_k_ff_6 (
    .J(and_10_out), .K(and_10_out), .clk(clock_1_out), .Q(j_k_ff_6_q), .preset(1'b0), .reset(or_1_out));  // open: Qn
  and and_11 (and_11_out, and_9_out, j_k_ff_6_q);
  J_K_Flip_Flop j_k_ff_7 (
    .J(and_12_out), .K(and_12_out), .clk(clock_1_out), .Q(j_k_ff_7_q), .preset(1'b0), .reset(or_1_out));  // open: Qn
  and and_12 (and_12_out, EN, and_11_out);
  and and_13 (and_13_out, ~j_k_ff_1_q, ~j_k_ff_2_q, j_k_ff_3_q, ~j_k_ff_4_q, ~j_k_ff_5_q, j_k_ff_6_q, j_k_ff_7_q);  // AND_Gate
  and and_14 (Output_1, j_k_ff_1_q, j_k_ff_2_q, ~j_k_ff_3_q, ~j_k_ff_4_q, ~j_k_ff_5_q, j_k_ff_6_q, j_k_ff_7_q);  // AND_Gate

  // Notes on the sheet:
  //   count to 100 - used for 1024Hz input
endmodule
