// Logisim project time.circ as structural Verilog: 4 circuits, main circuit seconds_counter
module seconds_counter (
  input  run_wk_s,
  input  CLK_input,
  input  run_st_s,
  output [3:0] s1_output,
  output s_c_out,
  output [3:0] s2_output
);

  wire and_1_out, counter_1_carry, or_1_out, or_2_out, out_1;

  and and_1 (and_1_out, run_st_s, CLK_input);
  or or_1 (or_1_out, and_1_out, out_1);
  Counter #(.width(4), .max('hf)) counter_1 (
    .clr(out_1), .count(run_wk_s), .clk(CLK_input), .carry(counter_1_carry), .Q(s1_output));  // open: load, up, D
  Counter #(.width(4), .max('hf)) counter_2 (
    .clr(s_c_out), .count(or_2_out), .clk(or_1_out), .Q(s2_output));  // open: load, up, D, carry
  or or_2 (or_2_out, run_st_s, out_1);
  and and_2 (out_1, s1_output[1], s1_output[3]);
  and and_3 (s_c_out, s2_output[1], s2_output[2]);

  // Other names for the same wires on the sheet: out_2 = s_c_out; str_scnd[3:0] = s2_output
endmodule

module date (
  input  set_mode,
  input  in_2
);

  wire and_1_out, and_3_out, and_4_out, and_5_out, and_6_out, and_7_out, and_8_out, and_9_out, and_10_out,
       and_11_out, but_out, CLK, clock_1_out, demultiplexer_1_out0, demultiplexer_1_out1,
       demultiplexer_1_out2, demultiplexer_1_out3, demultiplexer_1_out4, demultiplexer_1_out5,
       minutes_counter_1_c_out, not_1_out, not_2_out, not_3_out, not_4_out, not_5_out, or_1_out, or_2_out,
       or_3_out, or_4_out, seconds_counter_1_s_c_out;
  wire [2:0] counter_1_q;
  wire [3:0] hours_counter_1_st_hr, hours_counter_1_wk_hr, minutes_counter_1_m1_out,
       minutes_counter_1_m2_out, multiplexer_1_out, multiplexer_2_out, multiplexer_3_out, multiplexer_4_out,
       multiplexer_5_out, multiplexer_6_out, seconds_counter_1_s1_output, seconds_counter_1_s2_output;

  Demultiplexer #(.select(3), .enable("false")) demultiplexer_1 (
    .out0(demultiplexer_1_out0), .out1(demultiplexer_1_out1), .out2(demultiplexer_1_out2),
    .out3(demultiplexer_1_out3), .out4(demultiplexer_1_out4), .out5(demultiplexer_1_out5), .in(in_2),
    .sel(counter_1_q));  // open: out6, out7
  Counter #(.width(3), .max('h5)) counter_1 (.clk(in_2), .Q(counter_1_q));  // open: clr, load, up, count, D, carry
  Button but (.out(but_out));
  Clock clock_1 (.out(clock_1_out));
  not not_1 (not_1_out, set_mode);
  or or_1 (or_1_out, not_1_out, but_out);
  not not_2 (not_2_out, set_mode);
  or or_2 (or_2_out, not_2_out, and_1_out);
  and and_1 (and_1_out, set_mode, demultiplexer_1_out0);
  and and_2 (CLK, or_1_out, clock_1_out);
  and and_3 (and_3_out, set_mode, demultiplexer_1_out1);
  and and_4 (and_4_out, demultiplexer_1_out2, set_mode);
  and and_5 (and_5_out, and_4_out, set_mode);
  and and_6 (and_6_out, demultiplexer_1_out3, set_mode);
  and and_7 (and_7_out, demultiplexer_1_out5, set_mode);
  or or_3 (or_3_out, and_10_out, and_5_out);
  buf or_4 (or_4_out, and_11_out);  // OR_Gate
  and and_8 (and_8_out, demultiplexer_1_out4, set_mode);
  and and_9 (and_9_out, set_mode, clock_1_out);
  and and_10 (and_10_out, not_4_out, seconds_counter_1_s_c_out);
  and and_11 (and_11_out, not_5_out, minutes_counter_1_c_out);
  not not_3 (not_3_out, and_9_out);
  seconds_counter seconds_counter_1 (
    .run_wk_s(or_2_out), .CLK_input(CLK), .run_st_s(and_3_out), .s1_output(seconds_counter_1_s1_output),
    .s_c_out(seconds_counter_1_s_c_out), .s2_output(seconds_counter_1_s2_output));
  not not_4 (not_4_out, set_mode);
  minutes_counter minutes_counter_1 (
    .run_wk_mn(or_3_out), .c_in(and_10_out), .CLK_input(CLK), .run_st_mn(and_6_out),
    .m1_out(minutes_counter_1_m1_out), .m2_out(minutes_counter_1_m2_out), .c_out(minutes_counter_1_c_out));
  not not_5 (not_5_out, set_mode);
  hours_counter hours_counter_1 (
    .run_st_hr(and_7_out), .run_wk_hr(and_8_out), .c_in(or_4_out), .CLK_input(CLK),
    .st_hr(hours_counter_1_st_hr), .wk_hr(hours_counter_1_wk_hr));
  Hex_Digit_Display hex_digit_display_1 (.value(multiplexer_2_out));  // open: dp
  Hex_Digit_Display hex_digit_display_2 (.value(multiplexer_1_out));  // open: dp
  Multiplexer #(.width(4), .enable("false")) multiplexer_1 (
    .in1(hours_counter_1_wk_hr), .out(multiplexer_1_out), .sel(not_3_out));  // open: in0
  Multiplexer #(.width(4), .enable("false")) multiplexer_2 (
    .in1(hours_counter_1_st_hr), .out(multiplexer_2_out), .sel(not_3_out));  // open: in0
  Hex_Digit_Display hex_digit_display_3 (.value(multiplexer_3_out));  // open: dp
  Multiplexer #(.width(4), .enable("false")) multiplexer_3 (
    .in1(minutes_counter_1_m2_out), .out(multiplexer_3_out), .sel(not_3_out));  // open: in0
  Hex_Digit_Display hex_digit_display_4 (.value(multiplexer_4_out));  // open: dp
  Multiplexer #(.width(4), .enable("false")) multiplexer_4 (
    .in1(minutes_counter_1_m1_out), .out(multiplexer_4_out), .sel(not_3_out));  // open: in0
  Hex_Digit_Display hex_digit_display_5 (.value(multiplexer_5_out));  // open: dp
  Multiplexer #(.width(4), .enable("false")) multiplexer_5 (
    .in1(seconds_counter_1_s2_output), .out(multiplexer_5_out), .sel(not_3_out));  // open: in0
  Hex_Digit_Display hex_digit_display_6 (.value(multiplexer_6_out));  // open: dp
  Multiplexer #(.width(4), .enable("false")) multiplexer_6 (
    .in1(seconds_counter_1_s1_output), .out(multiplexer_6_out), .sel(not_3_out));  // open: in0

  // Other names for the same wires on the sheet: set_m = set_mode
endmodule

module minutes_counter (
  input  run_wk_mn,
  input  c_in,
  input  CLK_input,
  input  run_st_mn,
  output [3:0] m1_out,
  output [3:0] m2_out,
  output c_out
);

  wire and_1_out, and_2_out, or_1_out, or_2_out, or_3_out, out_4;

  and and_1 (and_1_out, run_st_mn, CLK_input);
  Counter #(.width(4), .max('hf)) counter_1 (
    .clr(out_4), .count(run_wk_mn), .clk(or_1_out), .Q(m1_out));  // open: load, up, D, carry
  or or_1 (or_1_out, c_in, and_2_out);
  and and_2 (and_2_out, run_wk_mn, CLK_input);
  Counter #(.width(4), .max('hf)) counter_2 (
    .clr(c_out), .count(or_2_out), .clk(or_3_out), .Q(m2_out));  // open: load, up, D, carry
  or or_2 (or_2_out, run_st_mn, out_4);
  or or_3 (or_3_out, and_1_out, out_4);
  and and_3 (out_4, m1_out[3], m1_out[1]);
  and and_4 (c_out, m2_out[2], m2_out[1]);

  // Other names for the same wires on the sheet: out_5 = c_out; str_min[3:0] = m2_out
endmodule

module hours_counter (
  input  run_st_hr,
  input  run_wk_hr,
  input  c_in,
  input  CLK_input,
  output [3:0] st_hr,
  output [3:0] wk_hr
);

  wire and_1_out, and_2_out, and_4_out, and_5_out, and_6_out, and_7_out, or_1_out, or_2_out, or_3_out,
       or_4_out, or_5_out, or_6_out, out_6, out_7, reset;

  and and_1 (and_1_out, run_st_hr, CLK_input);
  and and_2 (and_2_out, run_wk_hr, CLK_input);
  Counter #(.width(4), .max('hf)) counter_1 (
    .clr(or_1_out), .count(or_2_out), .clk(or_3_out), .Q(st_hr));  // open: load, up, D, carry
  or or_1 (or_1_out, reset, out_7);
  buf or_2 (or_2_out, run_st_hr);  // OR_Gate
  or or_3 (or_3_out, out_6, and_1_out);
  or or_4 (or_4_out, reset, out_6);
  or or_5 (or_5_out, run_wk_hr, c_in);
  or or_6 (or_6_out, c_in, and_2_out);
  Counter #(.width(4), .max('hf)) counter_2 (
    .clr(or_4_out), .count(or_5_out), .clk(or_6_out), .Q(wk_hr));  // open: load, up, D, carry
  or or_7 (reset, and_4_out, and_5_out, and_6_out);
  and and_3 (out_7, st_hr[0], st_hr[1]);
  and and_4 (and_4_out, wk_hr[2], st_hr[1]);
  and and_5 (and_5_out, st_hr[1], wk_hr[3]);
  and and_6 (and_6_out, st_hr[1], and_7_out);
  and and_7 (and_7_out, wk_hr[3], wk_hr[0]);
  and and_8 (out_6, wk_hr[1], wk_hr[3]);
endmodule
